// Logisim project 32bALU.circ as structural Verilog: 28 circuits, main circuit Clink
module main (
  input  [31:0] in1,
  input  [3:0] selec,
  input  [31:0] in2,
  output [31:0] out1
);

  wire [31:0] and_1_c, div32_1_p3, nor_1_c, not_1_b, or_1_c, plus32_1_s, plus32_2_s, sdiv32_1_out_3,
       shifterl_1_c, shifterr_1_output, shifterr_2_output, smult32_1_out_3, xor_1_c;
  wire [63:0] mult32_1_q;

  plus32 plus32_1 (.A(in1), .B(in2), .S(plus32_1_s));  // open: SUB, C
  plus32 plus32_2 (.A(in1), .B(in2), .SUB(1'b1), .S(plus32_2_s));  // open: C
  MULT32 mult32_1 (.A(in1), .B(in2), .Q(mult32_1_q));
  smult32 smult32_1 (.A(in1), .B(in2), .out_3(smult32_1_out_3));
  // Div32 div32_1: pin names not known; wires that end beside it: in2, in1, div32_1_p3
  sDiv32 sdiv32_1 (.A(in1), .B(in2), .out_3(sdiv32_1_out_3));
  OR or_1 (.A(in1), .B(in2), .C(or_1_c));
  NOT not_1 (.A(in1), .B(not_1_b));
  XOR xor_1 (.A(in1), .B(in2), .C(xor_1_c));
  AND and_1 (.A(in1), .B(in2), .C(and_1_c));
  NOR nor_1 (.A(in1), .B(in2), .C(nor_1_c));
  shifterL shifterl_1 (.Sa(in2[4:0]), .B(in1), .C(shifterl_1_c));  // open: Cin
  shifterR shifterr_1 (.Sa(in2[4:0]), .Input(in1), .OUTPUT(shifterr_1_output));  // open: logi
  shifterR shifterr_2 (.Sa(in2[4:0]), .Input(in1), .logi(in1[31]), .OUTPUT(shifterr_2_output));
  Multiplexer #(.select(4), .width(32)) multiplexer_1 (
    .in0(plus32_1_s), .in1(plus32_2_s), .in2(mult32_1_q[31:0]), .in3(smult32_1_out_3), .in4(div32_1_p3),
    .in5(sdiv32_1_out_3), .in6(or_1_c), .in7(not_1_b), .in8(xor_1_c), .in9(and_1_c), .in10(nor_1_c),
    .in11(shifterl_1_c), .in12(shifterr_1_output), .in13(shifterr_2_output), .out(out1), .sel(selec));  // open: in14, in15
endmodule

module Clink (
  input  [7:0] D,
  input  CI,
  input  [7:0] T,
  output L_C7_8a4509e8,
  output L_C6_740847e7,
  output L_C5_3e858d4c,
  output L_C4_0ebe26e6,
  output L_C3_5c5fddbc,
  output L_C2_2f6e58ae,
  output L_C1_cd0fa8c4,
  output L_C0_abdca778
);

  wire and_1_out, and_2_out, and_3_out, and_4_out, and_5_out, and_6_out, and_7_out, and_8_out, and_9_out,
       and_10_out, and_11_out, and_12_out, and_13_out, and_14_out, and_15_out, and_16_out, and_17_out,
       and_18_out, and_19_out, and_20_out, and_21_out, and_22_out, and_23_out, and_24_out, and_25_out,
       and_26_out, and_27_out, and_28_out, and_29_out, and_30_out, and_31_out, and_32_out, and_33_out,
       and_34_out, and_35_out, and_36_out;

  and and_1 (and_1_out, T[7], D[6]);
  and and_2 (and_2_out, T[7], T[6], D[5]);
  and and_3 (and_3_out, T[7], T[6], T[5], D[4]);
  nor C7 (L_C7_8a4509e8, D[7], and_1_out, and_2_out, and_3_out, and_4_out, and_5_out, and_6_out, and_7_out, and_8_out);
  and and_4 (and_4_out, T[7], T[6], T[5], T[4], D[3]);
  and and_5 (and_5_out, T[7], T[6], T[5], T[4], T[3], D[2]);
  and and_6 (and_6_out, T[7], T[6], T[5], T[4], T[3], T[2], D[1]);
  and and_7 (and_7_out, T[7], T[6], T[5], T[4], T[3], T[2], T[1], D[0]);
  and and_8 (and_8_out, T[7], T[6], T[5], T[4], T[3], T[2], T[1], T[0], CI);
  and and_9 (and_9_out, T[6], T[5], D[4]);
  and and_10 (and_10_out, T[6], D[5]);
  nor C6 (L_C6_740847e7, D[6], and_10_out, and_9_out, and_11_out, and_12_out, and_13_out, and_14_out, and_15_out);
  and and_11 (and_11_out, T[6], T[5], T[4], D[3]);
  and and_12 (and_12_out, T[6], T[5], T[4], T[3], D[2]);
  and and_13 (and_13_out, T[6], T[5], T[4], T[3], T[2], D[1]);
  and and_14 (and_14_out, T[6], T[5], T[4], T[3], T[2], T[1], D[0]);
  and and_15 (and_15_out, T[6], T[5], T[4], T[3], T[2], T[1], T[0], CI);
  and and_16 (and_16_out, T[5], D[4]);
  and and_17 (and_17_out, T[5], T[4], D[3]);
  nor C5 (L_C5_3e858d4c, D[5], and_16_out, and_17_out, and_18_out, and_19_out, and_20_out, and_21_out);
  and and_18 (and_18_out, T[5], T[4], T[3], D[2]);
  and and_19 (and_19_out, T[5], T[4], T[3], T[2], D[1]);
  and and_20 (and_20_out, T[5], T[4], T[3], T[2], T[1], D[0]);
  and and_21 (and_21_out, T[5], T[4], T[3], T[2], T[1], T[0], CI);
  and and_22 (and_22_out, T[4], D[3]);
  and and_23 (and_23_out, T[4], T[3], D[2]);
  nor C4 (L_C4_0ebe26e6, D[4], and_22_out, and_23_out, and_24_out, and_25_out, and_26_out);
  and and_24 (and_24_out, T[4], T[3], T[2], D[1]);
  and and_25 (and_25_out, T[4], T[3], T[2], T[1], D[0]);
  and and_26 (and_26_out, T[4], T[3], T[2], T[1], T[0], CI);
  and and_27 (and_27_out, T[3], D[2]);
  nor C3 (L_C3_5c5fddbc, D[3], and_27_out, and_28_out, and_29_out, and_30_out);
  and and_28 (and_28_out, T[3], T[2], D[1]);
  and and_29 (and_29_out, T[3], T[2], T[1], D[0]);
  and and_30 (and_30_out, T[3], T[2], T[1], T[0], CI);
  and and_31 (and_31_out, T[2], D[1]);
  nor C2 (L_C2_2f6e58ae, D[2], and_31_out, and_32_out, and_33_out);
  and and_32 (and_32_out, T[2], T[1], D[0]);
  and and_33 (and_33_out, T[2], T[1], T[0], CI);
  nor C1 (L_C1_cd0fa8c4, D[1], and_34_out, and_35_out);
  and and_34 (and_34_out, T[1], D[0]);
  nor C0 (L_C0_abdca778, D[0], and_36_out);
  and and_35 (and_35_out, T[1], T[0], CI);
  and and_36 (and_36_out, T[0], CI);

  // Notes on the sheet:
  //   D: pull=down
  //   T: pull=down
  //   L_C7_8a4509e8: pull=up
  //   L_C6_740847e7: pull=up
  //   L_C5_3e858d4c: pull=up
  //   L_C4_0ebe26e6: pull=up
  //   L_C3_5c5fddbc: pull=up
  //   L_C2_2f6e58ae: pull=up
  //   L_C1_cd0fa8c4: pull=up
  //   L_C0_abdca778: pull=up
endmodule

module plus (
  input  A,
  input  B,
  input  Ci,
  output out_4
);

  wire nand_1_out, nand_2_out, nand_3_out, nand_4_out, nand_5_out, nand_6_out, nand_8_out;

  nand nand_1 (nand_1_out, A, nand_2_out);
  nand nand_2 (nand_2_out, A, B);
  nand nand_3 (nand_3_out, nand_2_out, B);
  nand nand_4 (nand_4_out, nand_1_out, nand_3_out);
  nand nand_5 (nand_5_out, nand_4_out, Ci);
  nand nand_6 (nand_6_out, nand_4_out, nand_5_out);
  nand nand_7 (out_4, nand_6_out, nand_8_out);
  nand nand_8 (nand_8_out, nand_5_out, Ci);

  // Notes on the sheet:
  //   A: pull=down
  //   B: pull=down
  //   Ci: pull=down
  //   out_4: pull=down
endmodule

module plus32 (
  input  [31:0] A,
  input  [31:0] B,
  input  SUB,
  output [31:0] S,
  output C
);

  wire plus8_1_co, plus8_2_co, plus8_3_co;
  wire [31:0] bit_extender_1_out, D_out, nand_1_out, nand_2_out, nand_3_out, nand_4_out, T_out, xor_1_out;

  assign bit_extender_1_out = {{31{SUB}}, SUB};  // Bit_Extender bit_extender_1
  assign xor_1_out = B ^ bit_extender_1_out;  // XOR_Gate xor_1, 32 bits wide
  assign nand_1_out = ~(A & xor_1_out);  // NAND_Gate nand_1, 32 bits wide
  assign nand_2_out = ~(A & nand_3_out);  // NAND_Gate nand_2, 32 bits wide
  assign nand_3_out = ~(A & xor_1_out);  // NAND_Gate nand_3, 32 bits wide
  assign nand_4_out = ~(nand_3_out & xor_1_out);  // NAND_Gate nand_4, 32 bits wide
  assign D_out = ~(nand_1_out & nand_1_out);  // NAND_Gate D, 32 bits wide
  assign T_out = ~(nand_2_out & nand_4_out);  // NAND_Gate T, 32 bits wide
  plus8 plus8_1 (
    .D(D_out[7:0]), .T(T_out[7:0]), .Ci(SUB), .A(A[7:0]), .B(xor_1_out[7:0]), .out_6(S[7:0]), .Co(plus8_1_co));
  plus8 plus8_2 (
    .D(D_out[15:8]), .T(T_out[15:8]), .Ci(plus8_1_co), .A(A[15:8]), .B(xor_1_out[15:8]), .out_6(S[15:8]),
    .Co(plus8_2_co));
  plus8 plus8_3 (
    .D(D_out[23:16]), .T(T_out[23:16]), .Ci(plus8_2_co), .A(A[23:16]), .B(xor_1_out[23:16]),
    .out_6(S[23:16]), .Co(plus8_3_co));
  plus8 plus8_4 (
    .D(D_out[31:24]), .T(T_out[31:24]), .Ci(plus8_3_co), .A(A[31:24]), .B(xor_1_out[31:24]),
    .out_6(S[31:24]), .Co(C));

  // Notes on the sheet:
  //   B: pull=down
  //   A: pull=down
  //   C: pull=down
  //   S: pull=down
  //   D
  //   T
endmodule

module plus8 (
  input  [7:0] D,
  input  [7:0] T,
  input  Ci,
  input  [7:0] A,
  input  [7:0] B,
  output [7:0] out_6,
  output Co
);

  wire clink_1_l_c0_abdca778, clink_1_l_c1_cd0fa8c4, clink_1_l_c2_2f6e58ae, clink_1_l_c3_5c5fddbc,
       clink_1_l_c4_0ebe26e6, clink_1_l_c5_3e858d4c, clink_1_l_c6_740847e7, clink_1_l_c7_8a4509e8, not_2_out,
       not_3_out, not_4_out, not_5_out, not_6_out, not_7_out, not_8_out;

  Clink clink_1 (
    .D(D), .CI(Ci), .T(T), .L_C7_8a4509e8(clink_1_l_c7_8a4509e8), .L_C6_740847e7(clink_1_l_c6_740847e7),
    .L_C5_3e858d4c(clink_1_l_c5_3e858d4c), .L_C4_0ebe26e6(clink_1_l_c4_0ebe26e6),
    .L_C3_5c5fddbc(clink_1_l_c3_5c5fddbc), .L_C2_2f6e58ae(clink_1_l_c2_2f6e58ae),
    .L_C1_cd0fa8c4(clink_1_l_c1_cd0fa8c4), .L_C0_abdca778(clink_1_l_c0_abdca778));
  not not_1 (Co, clink_1_l_c7_8a4509e8);
  not not_2 (not_2_out, clink_1_l_c6_740847e7);
  not not_3 (not_3_out, clink_1_l_c5_3e858d4c);
  not not_4 (not_4_out, clink_1_l_c4_0ebe26e6);
  not not_5 (not_5_out, clink_1_l_c3_5c5fddbc);
  not not_6 (not_6_out, clink_1_l_c2_2f6e58ae);
  not not_7 (not_7_out, clink_1_l_c1_cd0fa8c4);
  not not_8 (not_8_out, clink_1_l_c0_abdca778);
  plus plus_1 (.A(B[0]), .B(A[0]), .Ci(Ci), .out_4(out_6[0]));
  plus plus_2 (.A(B[1]), .B(A[1]), .Ci(not_8_out), .out_4(out_6[1]));
  plus plus_3 (.A(B[2]), .B(A[2]), .Ci(not_7_out), .out_4(out_6[2]));
  plus plus_4 (.A(B[3]), .B(A[3]), .Ci(not_6_out), .out_4(out_6[3]));
  plus plus_5 (.A(B[4]), .B(A[4]), .Ci(not_5_out), .out_4(out_6[4]));
  plus plus_6 (.A(B[5]), .B(A[5]), .Ci(not_4_out), .out_4(out_6[5]));
  plus plus_7 (.A(B[6]), .B(A[6]), .Ci(not_3_out), .out_4(out_6[6]));
  plus plus_8 (.A(B[7]), .B(A[7]), .Ci(not_2_out), .out_4(out_6[7]));

  // Notes on the sheet:
  //   out_6: pull=down
  //   Co: pull=down
  //   A: pull=down
  //   Ci: pull=down
  //   D: pull=down
  //   T: pull=down
  //   B: pull=down
endmodule

module HA (
  input  A,
  input  B,
  output S,
  output C
);

  xor xor_1 (S, A, B);
  and and_1 (C, B, A);
endmodule

module FA (
  input  CIN,
  input  X,
  input  Y,
  output Sum,
  output Carry
);

  wire ha_1_c, ha_1_s, ha_2_c;

  HA ha_1 (.A(X), .B(Y), .S(ha_1_s), .C(ha_1_c));
  HA ha_2 (.A(CIN), .B(ha_1_s), .S(Sum), .C(ha_2_c));
  or or_1 (Carry, ha_2_c, ha_1_c);
endmodule

module mult4 (
  input  [3:0] A,
  input  [3:0] B,
  output [7:0] Q
);

  wire fa_1_carry, fa_1_sum, fa_3_carry, fa_3_sum, fa_4_carry, fa_5_carry, fa_5_sum, fa_6_carry, fa_6_sum,
       fa_7_carry, fa_7_sum, fa_8_carry, ha_1_c, ha_1_s, ha_2_c, ha_3_c, ha_4_c, P01_out, P02_out, P03_out,
       P10_out, P11_out, P12_out, P13_out, P20_out, P21_out, P22_out, P23_out, P30_out, P31_out, P32_out,
       P33_out;

  and P33 (P33_out, B[3], A[3]);
  and P32 (P32_out, B[2], A[3]);
  and P31 (P31_out, B[1], A[3]);
  FA fa_1 (.CIN(ha_1_c), .X(P23_out), .Y(P32_out), .Sum(fa_1_sum), .Carry(fa_1_carry));
  FA fa_2 (.CIN(fa_4_carry), .X(fa_1_carry), .Y(P33_out), .Sum(Q[6]), .Carry(Q[7]));
  and P30 (P30_out, B[0], A[3]);
  and P23 (P23_out, B[3], A[2]);
  and P22 (P22_out, B[2], A[2]);
  HA ha_1 (.A(P13_out), .B(P22_out), .S(ha_1_s), .C(ha_1_c));
  FA fa_3 (.CIN(fa_5_carry), .X(ha_1_s), .Y(P31_out), .Sum(fa_3_sum), .Carry(fa_3_carry));
  FA fa_4 (.CIN(fa_8_carry), .X(fa_3_carry), .Y(fa_1_sum), .Sum(Q[5]), .Carry(fa_4_carry));
  and P21 (P21_out, B[1], A[2]);
  and P20 (P20_out, B[0], A[2]);
  FA fa_5 (.CIN(P03_out), .X(P12_out), .Y(P21_out), .Sum(fa_5_sum), .Carry(fa_5_carry));
  and P13 (P13_out, B[3], A[1]);
  and P12 (P12_out, B[2], A[1]);
  FA fa_6 (.CIN(fa_7_carry), .X(fa_5_sum), .Y(P30_out), .Sum(fa_6_sum), .Carry(fa_6_carry));
  and P11 (P11_out, B[1], A[1]);
  and P10 (P10_out, B[0], A[1]);
  FA fa_7 (.CIN(P02_out), .X(P11_out), .Y(P20_out), .Sum(fa_7_sum), .Carry(fa_7_carry));
  FA fa_8 (.CIN(ha_2_c), .X(fa_6_carry), .Y(fa_3_sum), .Sum(Q[4]), .Carry(fa_8_carry));
  and P03 (P03_out, B[3], A[0]);
  HA ha_2 (.A(ha_4_c), .B(fa_6_sum), .S(Q[3]), .C(ha_2_c));
  and P02 (P02_out, B[2], A[0]);
  and P01 (P01_out, B[1], A[0]);
  HA ha_3 (.A(P01_out), .B(P10_out), .S(Q[1]), .C(ha_3_c));
  HA ha_4 (.A(ha_3_c), .B(fa_7_sum), .S(Q[2]), .C(ha_4_c));
  and P00 (Q[0], B[0], A[0]);
endmodule

module mult8 (
  input  [7:0] A,
  input  [7:0] B,
  output [15:0] Q
);

  wire add8_1_co, add8_2_co, undriven;
  wire [3:0] add4_1_1_s;
  wire [7:0] add8_1_s, mult4_2_q, mult4_3_q, mult4_4_q;
  wire [7:4] mult4_1_q;

  mult4 mult4_1 (.A(A[3:0]), .B(B[3:0]), .Q({mult4_1_q, Q[3:0]}));
  mult4 mult4_2 (.A(A[3:0]), .B(B[7:4]), .Q(mult4_2_q));
  mult4 mult4_3 (.A(A[7:4]), .B(B[3:0]), .Q(mult4_3_q));
  mult4 mult4_4 (.A(A[7:4]), .B(B[7:4]), .Q(mult4_4_q));
  add8 add8_1 (.C(1'b0), .A(mult4_2_q), .B(mult4_3_q), .CO(add8_1_co), .S(add8_1_s));
  add8 add8_2 (.C(undriven), .A({mult4_4_q[3:0], mult4_1_q}), .B(add8_1_s), .CO(add8_2_co), .S(Q[11:4]));
  add4_1 add4_1_1 (.B(add8_1_co), .A(mult4_4_q[7:4]), .S(add4_1_1_s));  // open: CO
  add4_1 add4_1_2 (.B(add8_2_co), .A(add4_1_1_s), .S(Q[15:12]));  // open: CO
endmodule

module add8 (
  input  C,
  input  [7:0] A,
  input  [7:0] B,
  output CO,
  output [7:0] S
);

  wire fa_1_carry, fa_2_carry, fa_3_carry, fa_4_carry, fa_5_carry, fa_6_carry, fa_7_carry;

  FA fa_1 (.CIN(C), .X(A[0]), .Y(B[0]), .Sum(S[0]), .Carry(fa_1_carry));
  FA fa_2 (.CIN(fa_1_carry), .X(A[1]), .Y(B[1]), .Sum(S[1]), .Carry(fa_2_carry));
  FA fa_3 (.CIN(fa_2_carry), .X(A[2]), .Y(B[2]), .Sum(S[2]), .Carry(fa_3_carry));
  FA fa_4 (.CIN(fa_3_carry), .X(A[3]), .Y(B[3]), .Sum(S[3]), .Carry(fa_4_carry));
  FA fa_5 (.CIN(fa_4_carry), .X(A[4]), .Y(B[4]), .Sum(S[4]), .Carry(fa_5_carry));
  FA fa_6 (.CIN(fa_5_carry), .X(A[5]), .Y(B[5]), .Sum(S[5]), .Carry(fa_6_carry));
  FA fa_7 (.CIN(fa_6_carry), .X(A[6]), .Y(B[6]), .Sum(S[6]), .Carry(fa_7_carry));
  FA fa_8 (.CIN(fa_7_carry), .X(A[7]), .Y(B[7]), .Sum(S[7]), .Carry(CO));
endmodule

module add16 (
  input  CI,
  input  [15:0] A,
  input  [15:0] B,
  output [15:0] S,
  output CO
);

  wire add8_1_co;

  add8 add8_1 (.C(CI), .A(A[7:0]), .B(B[7:0]), .CO(add8_1_co), .S(S[7:0]));
  add8 add8_2 (.C(add8_1_co), .A(A[15:8]), .B(B[15:8]), .CO(CO), .S(S[15:8]));
endmodule

module add4_1 (
  input  B,
  input  [3:0] A,
  output CO,
  output [3:0] S
);

  wire ha_1_c, ha_2_c, ha_3_c;

  HA ha_1 (.A(B), .B(A[0]), .S(S[0]), .C(ha_1_c));
  HA ha_2 (.A(ha_1_c), .B(A[1]), .S(S[1]), .C(ha_2_c));
  HA ha_3 (.A(ha_2_c), .B(A[2]), .S(S[2]), .C(ha_3_c));
  HA ha_4 (.A(ha_3_c), .B(A[3]), .S(S[3]), .C(CO));
endmodule

module mult16 (
  input  [15:0] A,
  input  [15:0] B,
  output [31:0] Q
);

  wire add8_2_co, add16_1_co;
  wire [7:0] add8_1_1_q;
  wire [15:0] add16_1_s, mult8_2_q, mult8_3_q, mult8_4_q;
  wire [15:8] mult8_1_q;

  mult8 mult8_1 (.A(A[7:0]), .B(B[7:0]), .Q({mult8_1_q, Q[7:0]}));
  mult8 mult8_2 (.A(A[7:0]), .B(B[15:8]), .Q(mult8_2_q));
  mult8 mult8_3 (.A(A[15:8]), .B(B[7:0]), .Q(mult8_3_q));
  mult8 mult8_4 (.A(A[15:8]), .B(B[15:8]), .Q(mult8_4_q));
  add16 add16_1 (.A(mult8_2_q), .B(mult8_3_q), .S(add16_1_s), .CO(add16_1_co));  // open: CI
  add8 add8_1 (.A(mult8_1_q), .B(add16_1_s[7:0]), .S(Q[15:8]));  // open: C, CO
  add8 add8_2 (.A(add16_1_s[15:8]), .B(mult8_4_q[7:0]), .CO(add8_2_co), .S(Q[23:16]));  // open: C
  add8_1 add8_1_1 (.B(add8_2_co), .A(mult8_4_q[15:8]), .Q(add8_1_1_q));  // open: CO
  add8_1 add8_1_2 (.B(add16_1_co), .A(add8_1_1_q), .Q(Q[31:24]));  // open: CO
endmodule

module MULT32 (
  input  [31:0] A,
  input  [31:0] B,
  output [63:0] Q
);

  wire add16_2_co, plus32_1_c;
  wire [15:0] add16_1_1_q;
  wire [31:0] mult16_2_q, mult16_3_q, mult16_4_q, plus32_1_s;
  wire [31:16] mult16_1_q;

  mult16 mult16_1 (.A(A[15:0]), .B(B[15:0]), .Q({mult16_1_q, Q[15:0]}));
  mult16 mult16_2 (.A(A[15:0]), .B(B[31:16]), .Q(mult16_2_q));
  mult16 mult16_3 (.A(A[31:16]), .B(B[15:0]), .Q(mult16_3_q));
  mult16 mult16_4 (.A(A[31:16]), .B(B[31:16]), .Q(mult16_4_q));
  plus32 plus32_1 (.A(mult16_2_q), .B(mult16_3_q), .S(plus32_1_s), .C(plus32_1_c));  // open: SUB
  add16 add16_1 (.A(mult16_1_q), .B(plus32_1_s[15:0]), .S(Q[31:16]));  // open: CI, CO
  add16 add16_2 (.A(plus32_1_s[31:16]), .B(mult16_4_q[15:0]), .S(Q[47:32]), .CO(add16_2_co));  // open: CI
  add16_1 add16_1_1 (.B(add16_2_co), .in_2(mult16_4_q[31:16]), .Q(add16_1_1_q));  // open: CO
  mult8 mult8_1 ();  // open: A, B, Q
  add16_1 add16_1_2 (.B(plus32_1_c), .in_2(add16_1_1_q), .Q(Q[63:48]));  // open: CO
endmodule

module add8_1 (
  input  B,
  input  [7:0] A,
  output [7:0] Q,
  output CO
);

  wire add4_1_1_co;

  add4_1 add4_1_1 (.B(B), .A(A[3:0]), .CO(add4_1_1_co), .S(Q[3:0]));
  add4_1 add4_1_2 (.B(add4_1_1_co), .A(A[7:4]), .CO(CO), .S(Q[7:4]));
endmodule

module add16_1 (
  input  B,
  input  [15:0] in_2,
  output [15:0] Q,
  output CO
);

  wire add8_1_1_co;

  add8_1 add8_1_1 (.B(B), .A(in_2[7:0]), .CO(add8_1_1_co), .Q(Q[7:0]));
  add8_1 add8_1_2 (.B(add8_1_1_co), .A(in_2[15:8]), .CO(CO), .Q(Q[15:8]));
endmodule

module smult32 (
  input  [31:0] A,
  input  [31:0] B,
  output [31:0] out_3
);

  wire xor_3_out;
  wire [31:0] bit_extender_1_out, bit_extender_2_out, bit_extender_3_out, bit_extender_4_out,
       bit_extender_5_out, bit_extender_6_out, plus32_1_s, plus32_2_s, xor_1_out, xor_2_out, xor_4_out;
  wire [63:0] mult32_1_q;

  assign bit_extender_1_out = {{31{1'b0}}, A[31]};  // Bit_Extender bit_extender_1
  assign bit_extender_2_out = {{31{A[31]}}, A[31]};  // Bit_Extender bit_extender_2
  assign bit_extender_3_out = {{31{1'b0}}, B[31]};  // Bit_Extender bit_extender_3
  assign bit_extender_4_out = {{31{B[31]}}, B[31]};  // Bit_Extender bit_extender_4
  assign xor_1_out = bit_extender_2_out ^ A;  // XOR_Gate xor_1, 32 bits wide
  assign xor_2_out = bit_extender_4_out ^ B;  // XOR_Gate xor_2, 32 bits wide
  plus32 plus32_1 (.A(bit_extender_1_out), .B(xor_1_out), .S(plus32_1_s));  // open: SUB, C
  plus32 plus32_2 (.A(bit_extender_3_out), .B(xor_2_out), .S(plus32_2_s));  // open: SUB, C
  MULT32 mult32_1 (.A(plus32_1_s), .B(plus32_2_s), .Q(mult32_1_q));
  xor xor_3 (xor_3_out, A[31], B[31]);
  assign bit_extender_5_out = {{31{xor_3_out}}, xor_3_out};  // Bit_Extender bit_extender_5
  assign bit_extender_6_out = {{31{1'b0}}, xor_3_out};  // Bit_Extender bit_extender_6
  assign xor_4_out = mult32_1_q[31:0] ^ bit_extender_5_out;  // XOR_Gate xor_4, 32 bits wide
  plus32 plus32_3 (.A(xor_4_out), .B(bit_extender_6_out), .S(out_3));  // open: SUB, C
endmodule

module shifterL (
  input  [31:0] B,
  input  Cin,
  input  [4:0] Sa,
  output [31:0] C
);

  wire multiplexer_1_out, multiplexer_2_out, multiplexer_3_out, multiplexer_4_out, multiplexer_5_out,
       multiplexer_6_out, multiplexer_7_out, multiplexer_8_out, multiplexer_9_out, multiplexer_10_out,
       multiplexer_13_out, multiplexer_14_out, multiplexer_15_out, multiplexer_16_out, multiplexer_17_out,
       multiplexer_18_out, multiplexer_21_out, multiplexer_22_out, multiplexer_23_out, multiplexer_24_out,
       multiplexer_25_out, multiplexer_26_out, multiplexer_27_out, multiplexer_29_out, multiplexer_30_out,
       multiplexer_31_out, multiplexer_32_out, multiplexer_33_out, multiplexer_34_out, multiplexer_37_out,
       multiplexer_38_out, multiplexer_39_out, multiplexer_40_out, multiplexer_41_out, multiplexer_42_out,
       multiplexer_43_out, multiplexer_45_out, multiplexer_46_out, multiplexer_47_out, multiplexer_48_out,
       multiplexer_49_out, multiplexer_50_out, multiplexer_53_out, multiplexer_54_out, multiplexer_55_out,
       multiplexer_56_out, multiplexer_57_out, multiplexer_58_out, multiplexer_61_out, multiplexer_62_out,
       multiplexer_63_out, multiplexer_64_out, multiplexer_65_out, multiplexer_66_out, multiplexer_67_out,
       multiplexer_69_out, multiplexer_70_out, multiplexer_71_out, multiplexer_72_out, multiplexer_73_out,
       multiplexer_74_out, multiplexer_77_out, multiplexer_78_out, multiplexer_79_out, multiplexer_80_out,
       multiplexer_81_out, multiplexer_82_out, multiplexer_83_out, multiplexer_85_out, multiplexer_86_out,
       multiplexer_87_out, multiplexer_88_out, multiplexer_89_out, multiplexer_90_out, multiplexer_93_out,
       multiplexer_94_out, multiplexer_95_out, multiplexer_96_out, multiplexer_97_out, multiplexer_98_out,
       multiplexer_101_out, multiplexer_102_out, multiplexer_103_out, multiplexer_104_out,
       multiplexer_105_out, multiplexer_106_out, multiplexer_107_out, multiplexer_109_out,
       multiplexer_110_out, multiplexer_111_out, multiplexer_112_out, multiplexer_113_out,
       multiplexer_114_out, multiplexer_117_out, multiplexer_118_out, multiplexer_119_out,
       multiplexer_120_out, multiplexer_121_out, multiplexer_122_out, multiplexer_123_out,
       multiplexer_125_out, multiplexer_126_out, multiplexer_127_out, multiplexer_128_out,
       multiplexer_129_out, multiplexer_130_out, multiplexer_133_out, multiplexer_134_out,
       multiplexer_135_out, multiplexer_136_out, multiplexer_137_out, multiplexer_138_out,
       multiplexer_141_out, multiplexer_142_out, multiplexer_143_out, multiplexer_144_out,
       multiplexer_145_out, multiplexer_146_out, multiplexer_147_out, multiplexer_149_out,
       multiplexer_150_out, multiplexer_151_out, multiplexer_152_out, multiplexer_153_out,
       multiplexer_154_out, multiplexer_157_out, multiplexer_158_out, multiplexer_159_out;

  Multiplexer multiplexer_1 (.in0(B[31]), .in1(B[15]), .out(multiplexer_1_out), .sel(Sa[4]));
  Multiplexer multiplexer_2 (.in0(multiplexer_1_out), .in1(multiplexer_37_out), .out(multiplexer_2_out), .sel(Sa[3]));
  Multiplexer multiplexer_3 (.in0(multiplexer_2_out), .in1(multiplexer_23_out), .out(multiplexer_3_out), .sel(Sa[2]));
  Multiplexer multiplexer_4 (.in0(multiplexer_3_out), .in1(multiplexer_15_out), .out(multiplexer_4_out), .sel(Sa[1]));
  Multiplexer multiplexer_5 (.in0(B[30]), .in1(B[14]), .out(multiplexer_5_out), .sel(Sa[4]));
  Multiplexer multiplexer_6 (.in0(B[29]), .in1(B[13]), .out(multiplexer_6_out), .sel(Sa[4]));
  Multiplexer multiplexer_7 (.in0(multiplexer_5_out), .in1(multiplexer_45_out), .out(multiplexer_7_out), .sel(Sa[3]));
  Multiplexer multiplexer_8 (.in0(multiplexer_6_out), .in1(multiplexer_46_out), .out(multiplexer_8_out), .sel(Sa[3]));
  Multiplexer multiplexer_9 (.in0(multiplexer_7_out), .in1(multiplexer_24_out), .out(multiplexer_9_out), .sel(Sa[2]));
  Multiplexer multiplexer_10 (.in0(multiplexer_9_out), .in1(multiplexer_16_out), .out(multiplexer_10_out), .sel(Sa[1]));
  Multiplexer multiplexer_11 (.in0(multiplexer_4_out), .in1(multiplexer_10_out), .out(C[31]), .sel(Sa[0]));
  Multiplexer multiplexer_12 (.in0(multiplexer_10_out), .in1(multiplexer_17_out), .out(C[30]), .sel(Sa[0]));
  Multiplexer multiplexer_13 (.in0(B[28]), .in1(B[12]), .out(multiplexer_13_out), .sel(Sa[4]));
  Multiplexer multiplexer_14 (
    .in0(multiplexer_13_out), .in1(multiplexer_53_out), .out(multiplexer_14_out), .sel(Sa[3]));
  Multiplexer multiplexer_15 (.in0(multiplexer_8_out), .in1(multiplexer_31_out), .out(multiplexer_15_out), .sel(Sa[2]));
  Multiplexer multiplexer_16 (
    .in0(multiplexer_14_out), .in1(multiplexer_39_out), .out(multiplexer_16_out), .sel(Sa[2]));
  Multiplexer multiplexer_17 (
    .in0(multiplexer_15_out), .in1(multiplexer_25_out), .out(multiplexer_17_out), .sel(Sa[1]));
  Multiplexer multiplexer_18 (
    .in0(multiplexer_16_out), .in1(multiplexer_26_out), .out(multiplexer_18_out), .sel(Sa[1]));
  Multiplexer multiplexer_19 (.in0(multiplexer_17_out), .in1(multiplexer_18_out), .out(C[29]), .sel(Sa[0]));
  Multiplexer multiplexer_20 (.in0(multiplexer_18_out), .in1(multiplexer_27_out), .out(C[28]), .sel(Sa[0]));
  Multiplexer multiplexer_21 (.in0(B[27]), .in1(B[11]), .out(multiplexer_21_out), .sel(Sa[4]));
  Multiplexer multiplexer_22 (.in0(B[26]), .in1(B[10]), .out(multiplexer_22_out), .sel(Sa[4]));
  Multiplexer multiplexer_23 (
    .in0(multiplexer_21_out), .in1(multiplexer_61_out), .out(multiplexer_23_out), .sel(Sa[3]));
  Multiplexer multiplexer_24 (
    .in0(multiplexer_22_out), .in1(multiplexer_62_out), .out(multiplexer_24_out), .sel(Sa[3]));
  Multiplexer multiplexer_25 (
    .in0(multiplexer_23_out), .in1(multiplexer_38_out), .out(multiplexer_25_out), .sel(Sa[2]));
  Multiplexer multiplexer_26 (
    .in0(multiplexer_24_out), .in1(multiplexer_47_out), .out(multiplexer_26_out), .sel(Sa[2]));
  Multiplexer multiplexer_27 (
    .in0(multiplexer_25_out), .in1(multiplexer_32_out), .out(multiplexer_27_out), .sel(Sa[1]));
  Multiplexer multiplexer_28 (.in0(multiplexer_27_out), .in1(multiplexer_33_out), .out(C[27]), .sel(Sa[0]));
  Multiplexer multiplexer_29 (.in0(B[25]), .in1(B[9]), .out(multiplexer_29_out), .sel(Sa[4]));
  Multiplexer multiplexer_30 (.in0(B[24]), .in1(B[8]), .out(multiplexer_30_out), .sel(Sa[4]));
  Multiplexer multiplexer_31 (
    .in0(multiplexer_29_out), .in1(multiplexer_69_out), .out(multiplexer_31_out), .sel(Sa[3]));
  Multiplexer multiplexer_32 (
    .in0(multiplexer_31_out), .in1(multiplexer_48_out), .out(multiplexer_32_out), .sel(Sa[2]));
  Multiplexer multiplexer_33 (
    .in0(multiplexer_26_out), .in1(multiplexer_41_out), .out(multiplexer_33_out), .sel(Sa[1]));
  Multiplexer multiplexer_34 (
    .in0(multiplexer_32_out), .in1(multiplexer_40_out), .out(multiplexer_34_out), .sel(Sa[1]));
  Multiplexer multiplexer_35 (.in0(multiplexer_33_out), .in1(multiplexer_34_out), .out(C[26]), .sel(Sa[0]));
  Multiplexer multiplexer_36 (.in0(multiplexer_34_out), .in1(multiplexer_43_out), .out(C[25]), .sel(Sa[0]));
  Multiplexer multiplexer_37 (.in0(B[23]), .in1(B[7]), .out(multiplexer_37_out), .sel(Sa[4]));
  Multiplexer multiplexer_38 (
    .in0(multiplexer_37_out), .in1(multiplexer_77_out), .out(multiplexer_38_out), .sel(Sa[3]));
  Multiplexer multiplexer_39 (
    .in0(multiplexer_30_out), .in1(multiplexer_70_out), .out(multiplexer_39_out), .sel(Sa[3]));
  Multiplexer multiplexer_40 (
    .in0(multiplexer_38_out), .in1(multiplexer_63_out), .out(multiplexer_40_out), .sel(Sa[2]));
  Multiplexer multiplexer_41 (
    .in0(multiplexer_39_out), .in1(multiplexer_54_out), .out(multiplexer_41_out), .sel(Sa[2]));
  Multiplexer multiplexer_42 (
    .in0(multiplexer_40_out), .in1(multiplexer_55_out), .out(multiplexer_42_out), .sel(Sa[1]));
  Multiplexer multiplexer_43 (
    .in0(multiplexer_41_out), .in1(multiplexer_49_out), .out(multiplexer_43_out), .sel(Sa[1]));
  Multiplexer multiplexer_44 (.in0(multiplexer_43_out), .in1(multiplexer_42_out), .out(C[24]), .sel(Sa[0]));
  Multiplexer multiplexer_45 (.in0(B[22]), .in1(B[6]), .out(multiplexer_45_out), .sel(Sa[4]));
  Multiplexer multiplexer_46 (.in0(B[21]), .in1(B[5]), .out(multiplexer_46_out), .sel(Sa[4]));
  Multiplexer multiplexer_47 (
    .in0(multiplexer_45_out), .in1(multiplexer_85_out), .out(multiplexer_47_out), .sel(Sa[3]));
  Multiplexer multiplexer_48 (
    .in0(multiplexer_46_out), .in1(multiplexer_86_out), .out(multiplexer_48_out), .sel(Sa[3]));
  Multiplexer multiplexer_49 (
    .in0(multiplexer_47_out), .in1(multiplexer_64_out), .out(multiplexer_49_out), .sel(Sa[2]));
  Multiplexer multiplexer_50 (
    .in0(multiplexer_49_out), .in1(multiplexer_56_out), .out(multiplexer_50_out), .sel(Sa[1]));
  Multiplexer multiplexer_51 (.in0(multiplexer_42_out), .in1(multiplexer_50_out), .out(C[23]), .sel(Sa[0]));
  Multiplexer multiplexer_52 (.in0(multiplexer_50_out), .in1(multiplexer_57_out), .out(C[22]), .sel(Sa[0]));
  Multiplexer multiplexer_53 (.in0(B[20]), .in1(B[4]), .out(multiplexer_53_out), .sel(Sa[4]));
  Multiplexer multiplexer_54 (
    .in0(multiplexer_53_out), .in1(multiplexer_93_out), .out(multiplexer_54_out), .sel(Sa[3]));
  Multiplexer multiplexer_55 (
    .in0(multiplexer_48_out), .in1(multiplexer_71_out), .out(multiplexer_55_out), .sel(Sa[2]));
  Multiplexer multiplexer_56 (
    .in0(multiplexer_54_out), .in1(multiplexer_78_out), .out(multiplexer_56_out), .sel(Sa[2]));
  Multiplexer multiplexer_57 (
    .in0(multiplexer_55_out), .in1(multiplexer_65_out), .out(multiplexer_57_out), .sel(Sa[1]));
  Multiplexer multiplexer_58 (
    .in0(multiplexer_56_out), .in1(multiplexer_66_out), .out(multiplexer_58_out), .sel(Sa[1]));
  Multiplexer multiplexer_59 (.in0(multiplexer_57_out), .in1(multiplexer_58_out), .out(C[21]), .sel(Sa[0]));
  Multiplexer multiplexer_60 (.in0(multiplexer_58_out), .in1(multiplexer_67_out), .out(C[20]), .sel(Sa[0]));
  Multiplexer multiplexer_61 (.in0(B[19]), .in1(B[3]), .out(multiplexer_61_out), .sel(Sa[4]));
  Multiplexer multiplexer_62 (.in0(B[18]), .in1(B[2]), .out(multiplexer_62_out), .sel(Sa[4]));
  Multiplexer multiplexer_63 (
    .in0(multiplexer_61_out), .in1(multiplexer_101_out), .out(multiplexer_63_out), .sel(Sa[3]));
  Multiplexer multiplexer_64 (
    .in0(multiplexer_62_out), .in1(multiplexer_102_out), .out(multiplexer_64_out), .sel(Sa[3]));
  Multiplexer multiplexer_65 (
    .in0(multiplexer_63_out), .in1(multiplexer_79_out), .out(multiplexer_65_out), .sel(Sa[2]));
  Multiplexer multiplexer_66 (
    .in0(multiplexer_64_out), .in1(multiplexer_87_out), .out(multiplexer_66_out), .sel(Sa[2]));
  Multiplexer multiplexer_67 (
    .in0(multiplexer_65_out), .in1(multiplexer_72_out), .out(multiplexer_67_out), .sel(Sa[1]));
  Multiplexer multiplexer_68 (.in0(multiplexer_67_out), .in1(multiplexer_73_out), .out(C[19]), .sel(Sa[0]));
  Multiplexer multiplexer_69 (.in0(B[17]), .in1(B[1]), .out(multiplexer_69_out), .sel(Sa[4]));
  Multiplexer multiplexer_70 (.in0(B[16]), .in1(B[0]), .out(multiplexer_70_out), .sel(Sa[4]));
  Multiplexer multiplexer_71 (
    .in0(multiplexer_69_out), .in1(multiplexer_109_out), .out(multiplexer_71_out), .sel(Sa[3]));
  Multiplexer multiplexer_72 (
    .in0(multiplexer_71_out), .in1(multiplexer_88_out), .out(multiplexer_72_out), .sel(Sa[2]));
  Multiplexer multiplexer_73 (
    .in0(multiplexer_66_out), .in1(multiplexer_80_out), .out(multiplexer_73_out), .sel(Sa[1]));
  Multiplexer multiplexer_74 (
    .in0(multiplexer_72_out), .in1(multiplexer_81_out), .out(multiplexer_74_out), .sel(Sa[1]));
  Multiplexer multiplexer_75 (.in0(multiplexer_73_out), .in1(multiplexer_74_out), .out(C[18]), .sel(Sa[0]));
  Multiplexer multiplexer_76 (.in0(multiplexer_74_out), .in1(multiplexer_82_out), .out(C[17]), .sel(Sa[0]));
  Multiplexer multiplexer_77 (.in0(B[15]), .in1(Cin), .out(multiplexer_77_out), .sel(Sa[4]));
  Multiplexer multiplexer_78 (
    .in0(multiplexer_70_out), .in1(multiplexer_110_out), .out(multiplexer_78_out), .sel(Sa[3]));
  Multiplexer multiplexer_79 (
    .in0(multiplexer_77_out), .in1(multiplexer_117_out), .out(multiplexer_79_out), .sel(Sa[3]));
  Multiplexer multiplexer_80 (
    .in0(multiplexer_78_out), .in1(multiplexer_94_out), .out(multiplexer_80_out), .sel(Sa[2]));
  Multiplexer multiplexer_81 (
    .in0(multiplexer_79_out), .in1(multiplexer_103_out), .out(multiplexer_81_out), .sel(Sa[2]));
  Multiplexer multiplexer_82 (
    .in0(multiplexer_80_out), .in1(multiplexer_89_out), .out(multiplexer_82_out), .sel(Sa[1]));
  Multiplexer multiplexer_83 (
    .in0(multiplexer_81_out), .in1(multiplexer_95_out), .out(multiplexer_83_out), .sel(Sa[1]));
  Multiplexer multiplexer_84 (.in0(multiplexer_82_out), .in1(multiplexer_83_out), .out(C[16]), .sel(Sa[0]));
  Multiplexer multiplexer_85 (.in0(B[14]), .in1(Cin), .out(multiplexer_85_out), .sel(Sa[4]));
  Multiplexer multiplexer_86 (.in0(B[13]), .in1(Cin), .out(multiplexer_86_out), .sel(Sa[4]));
  Multiplexer multiplexer_87 (
    .in0(multiplexer_85_out), .in1(multiplexer_125_out), .out(multiplexer_87_out), .sel(Sa[3]));
  Multiplexer multiplexer_88 (
    .in0(multiplexer_86_out), .in1(multiplexer_126_out), .out(multiplexer_88_out), .sel(Sa[3]));
  Multiplexer multiplexer_89 (
    .in0(multiplexer_87_out), .in1(multiplexer_104_out), .out(multiplexer_89_out), .sel(Sa[2]));
  Multiplexer multiplexer_90 (
    .in0(multiplexer_89_out), .in1(multiplexer_96_out), .out(multiplexer_90_out), .sel(Sa[1]));
  Multiplexer multiplexer_91 (.in0(multiplexer_83_out), .in1(multiplexer_90_out), .out(C[15]), .sel(Sa[0]));
  Multiplexer multiplexer_92 (.in0(multiplexer_90_out), .in1(multiplexer_97_out), .out(C[14]), .sel(Sa[0]));
  Multiplexer multiplexer_93 (.in0(B[12]), .in1(Cin), .out(multiplexer_93_out), .sel(Sa[4]));
  Multiplexer multiplexer_94 (
    .in0(multiplexer_93_out), .in1(multiplexer_133_out), .out(multiplexer_94_out), .sel(Sa[3]));
  Multiplexer multiplexer_95 (
    .in0(multiplexer_88_out), .in1(multiplexer_111_out), .out(multiplexer_95_out), .sel(Sa[2]));
  Multiplexer multiplexer_96 (
    .in0(multiplexer_94_out), .in1(multiplexer_118_out), .out(multiplexer_96_out), .sel(Sa[2]));
  Multiplexer multiplexer_97 (
    .in0(multiplexer_95_out), .in1(multiplexer_105_out), .out(multiplexer_97_out), .sel(Sa[1]));
  Multiplexer multiplexer_98 (
    .in0(multiplexer_96_out), .in1(multiplexer_106_out), .out(multiplexer_98_out), .sel(Sa[1]));
  Multiplexer multiplexer_99 (.in0(multiplexer_97_out), .in1(multiplexer_98_out), .out(C[13]), .sel(Sa[0]));
  Multiplexer multiplexer_100 (.in0(multiplexer_98_out), .in1(multiplexer_107_out), .out(C[12]), .sel(Sa[0]));
  Multiplexer multiplexer_101 (.in0(B[11]), .in1(Cin), .out(multiplexer_101_out), .sel(Sa[4]));
  Multiplexer multiplexer_102 (.in0(B[10]), .in1(Cin), .out(multiplexer_102_out), .sel(Sa[4]));
  Multiplexer multiplexer_103 (
    .in0(multiplexer_101_out), .in1(multiplexer_141_out), .out(multiplexer_103_out), .sel(Sa[3]));
  Multiplexer multiplexer_104 (
    .in0(multiplexer_102_out), .in1(multiplexer_142_out), .out(multiplexer_104_out), .sel(Sa[3]));
  Multiplexer multiplexer_105 (
    .in0(multiplexer_103_out), .in1(multiplexer_119_out), .out(multiplexer_105_out), .sel(Sa[2]));
  Multiplexer multiplexer_106 (
    .in0(multiplexer_104_out), .in1(multiplexer_127_out), .out(multiplexer_106_out), .sel(Sa[2]));
  Multiplexer multiplexer_107 (
    .in0(multiplexer_105_out), .in1(multiplexer_112_out), .out(multiplexer_107_out), .sel(Sa[1]));
  Multiplexer multiplexer_108 (.in0(multiplexer_107_out), .in1(multiplexer_113_out), .out(C[11]), .sel(Sa[0]));
  Multiplexer multiplexer_109 (.in0(B[9]), .in1(Cin), .out(multiplexer_109_out), .sel(Sa[4]));
  Multiplexer multiplexer_110 (.in0(B[8]), .in1(Cin), .out(multiplexer_110_out), .sel(Sa[4]));
  Multiplexer multiplexer_111 (
    .in0(multiplexer_109_out), .in1(multiplexer_149_out), .out(multiplexer_111_out), .sel(Sa[3]));
  Multiplexer multiplexer_112 (
    .in0(multiplexer_111_out), .in1(multiplexer_128_out), .out(multiplexer_112_out), .sel(Sa[2]));
  Multiplexer multiplexer_113 (
    .in0(multiplexer_106_out), .in1(multiplexer_120_out), .out(multiplexer_113_out), .sel(Sa[1]));
  Multiplexer multiplexer_114 (
    .in0(multiplexer_112_out), .in1(multiplexer_121_out), .out(multiplexer_114_out), .sel(Sa[1]));
  Multiplexer multiplexer_115 (.in0(multiplexer_113_out), .in1(multiplexer_114_out), .out(C[10]), .sel(Sa[0]));
  Multiplexer multiplexer_116 (.in0(multiplexer_114_out), .in1(multiplexer_122_out), .out(C[9]), .sel(Sa[0]));
  Multiplexer multiplexer_117 (.in0(B[7]), .in1(Cin), .out(multiplexer_117_out), .sel(Sa[4]));
  Multiplexer multiplexer_118 (
    .in0(multiplexer_110_out), .in1(multiplexer_150_out), .out(multiplexer_118_out), .sel(Sa[3]));
  Multiplexer multiplexer_119 (.in0(multiplexer_117_out), .in1(Cin), .out(multiplexer_119_out), .sel(Sa[3]));
  Multiplexer multiplexer_120 (
    .in0(multiplexer_118_out), .in1(multiplexer_134_out), .out(multiplexer_120_out), .sel(Sa[2]));
  Multiplexer multiplexer_121 (
    .in0(multiplexer_119_out), .in1(multiplexer_143_out), .out(multiplexer_121_out), .sel(Sa[2]));
  Multiplexer multiplexer_122 (
    .in0(multiplexer_120_out), .in1(multiplexer_129_out), .out(multiplexer_122_out), .sel(Sa[1]));
  Multiplexer multiplexer_123 (
    .in0(multiplexer_121_out), .in1(multiplexer_135_out), .out(multiplexer_123_out), .sel(Sa[1]));
  Multiplexer multiplexer_124 (.in0(multiplexer_122_out), .in1(multiplexer_123_out), .out(C[8]), .sel(Sa[0]));
  Multiplexer multiplexer_125 (.in0(B[6]), .in1(Cin), .out(multiplexer_125_out), .sel(Sa[4]));
  Multiplexer multiplexer_126 (.in0(B[5]), .in1(Cin), .out(multiplexer_126_out), .sel(Sa[4]));
  Multiplexer multiplexer_127 (.in0(multiplexer_125_out), .in1(Cin), .out(multiplexer_127_out), .sel(Sa[3]));
  Multiplexer multiplexer_128 (.in0(multiplexer_126_out), .in1(Cin), .out(multiplexer_128_out), .sel(Sa[3]));
  Multiplexer multiplexer_129 (
    .in0(multiplexer_127_out), .in1(multiplexer_144_out), .out(multiplexer_129_out), .sel(Sa[2]));
  Multiplexer multiplexer_130 (
    .in0(multiplexer_129_out), .in1(multiplexer_136_out), .out(multiplexer_130_out), .sel(Sa[1]));
  Multiplexer multiplexer_131 (.in0(multiplexer_123_out), .in1(multiplexer_130_out), .out(C[7]), .sel(Sa[0]));
  Multiplexer multiplexer_132 (.in0(multiplexer_130_out), .in1(multiplexer_137_out), .out(C[6]), .sel(Sa[0]));
  Multiplexer multiplexer_133 (.in0(B[4]), .in1(Cin), .out(multiplexer_133_out), .sel(Sa[4]));
  Multiplexer multiplexer_134 (.in0(multiplexer_133_out), .in1(Cin), .out(multiplexer_134_out), .sel(Sa[3]));
  Multiplexer multiplexer_135 (
    .in0(multiplexer_128_out), .in1(multiplexer_151_out), .out(multiplexer_135_out), .sel(Sa[2]));
  Multiplexer multiplexer_136 (
    .in0(multiplexer_134_out), .in1(multiplexer_157_out), .out(multiplexer_136_out), .sel(Sa[2]));
  Multiplexer multiplexer_137 (
    .in0(multiplexer_135_out), .in1(multiplexer_145_out), .out(multiplexer_137_out), .sel(Sa[1]));
  Multiplexer multiplexer_138 (
    .in0(multiplexer_136_out), .in1(multiplexer_146_out), .out(multiplexer_138_out), .sel(Sa[1]));
  Multiplexer multiplexer_139 (.in0(multiplexer_137_out), .in1(multiplexer_138_out), .out(C[5]), .sel(Sa[0]));
  Multiplexer multiplexer_140 (.in0(multiplexer_138_out), .in1(multiplexer_147_out), .out(C[4]), .sel(Sa[0]));
  Multiplexer multiplexer_141 (.in0(B[3]), .in1(Cin), .out(multiplexer_141_out), .sel(Sa[4]));
  Multiplexer multiplexer_142 (.in0(B[2]), .in1(Cin), .out(multiplexer_142_out), .sel(Sa[4]));
  Multiplexer multiplexer_143 (.in0(multiplexer_141_out), .in1(Cin), .out(multiplexer_143_out), .sel(Sa[3]));
  Multiplexer multiplexer_144 (.in0(multiplexer_142_out), .in1(Cin), .out(multiplexer_144_out), .sel(Sa[3]));
  Multiplexer multiplexer_145 (.in0(multiplexer_143_out), .in1(Cin), .out(multiplexer_145_out), .sel(Sa[2]));
  Multiplexer multiplexer_146 (.in0(multiplexer_144_out), .in1(Cin), .out(multiplexer_146_out), .sel(Sa[2]));
  Multiplexer multiplexer_147 (
    .in0(multiplexer_145_out), .in1(multiplexer_152_out), .out(multiplexer_147_out), .sel(Sa[1]));
  Multiplexer multiplexer_148 (.in0(multiplexer_147_out), .in1(multiplexer_153_out), .out(C[3]), .sel(Sa[0]));
  Multiplexer multiplexer_149 (.in0(B[1]), .in1(Cin), .out(multiplexer_149_out), .sel(Sa[4]));
  Multiplexer multiplexer_150 (.in0(B[0]), .in1(Cin), .out(multiplexer_150_out), .sel(Sa[4]));
  Multiplexer multiplexer_151 (.in0(multiplexer_149_out), .in1(Cin), .out(multiplexer_151_out), .sel(Sa[3]));
  Multiplexer multiplexer_152 (.in0(multiplexer_151_out), .in1(Cin), .out(multiplexer_152_out), .sel(Sa[2]));
  Multiplexer multiplexer_153 (
    .in0(multiplexer_146_out), .in1(multiplexer_158_out), .out(multiplexer_153_out), .sel(Sa[1]));
  Multiplexer multiplexer_154 (.in0(multiplexer_152_out), .in1(Cin), .out(multiplexer_154_out), .sel(Sa[1]));
  Multiplexer multiplexer_155 (.in0(multiplexer_153_out), .in1(multiplexer_154_out), .out(C[2]), .sel(Sa[0]));
  Multiplexer multiplexer_156 (.in0(multiplexer_154_out), .in1(multiplexer_159_out), .out(C[1]), .sel(Sa[0]));
  Multiplexer multiplexer_157 (.in0(multiplexer_150_out), .in1(Cin), .out(multiplexer_157_out), .sel(Sa[3]));
  Multiplexer multiplexer_158 (.in0(multiplexer_157_out), .in1(Cin), .out(multiplexer_158_out), .sel(Sa[2]));
  Multiplexer multiplexer_159 (.in0(multiplexer_158_out), .in1(Cin), .out(multiplexer_159_out), .sel(Sa[1]));
  Multiplexer multiplexer_160 (.in0(multiplexer_159_out), .in1(Cin), .out(C[0]), .sel(Sa[0]));
endmodule

module shifterR (
  input  [31:0] Input,
  input  logi,
  input  [4:0] Sa,
  output [31:0] OUTPUT
);

  wire multiplexer_1_out, multiplexer_2_out, multiplexer_3_out, multiplexer_4_out, multiplexer_5_out,
       multiplexer_6_out, multiplexer_7_out, multiplexer_8_out, multiplexer_9_out, multiplexer_10_out,
       multiplexer_11_out, multiplexer_12_out, multiplexer_15_out, multiplexer_16_out, multiplexer_17_out,
       multiplexer_18_out, multiplexer_19_out, multiplexer_20_out, multiplexer_21_out, multiplexer_22_out,
       multiplexer_25_out, multiplexer_26_out, multiplexer_27_out, multiplexer_28_out, multiplexer_29_out,
       multiplexer_30_out, multiplexer_31_out, multiplexer_32_out, multiplexer_35_out, multiplexer_36_out,
       multiplexer_37_out, multiplexer_38_out, multiplexer_39_out, multiplexer_40_out, multiplexer_41_out,
       multiplexer_42_out, multiplexer_45_out, multiplexer_46_out, multiplexer_47_out, multiplexer_48_out,
       multiplexer_49_out, multiplexer_50_out, multiplexer_51_out, multiplexer_52_out, multiplexer_55_out,
       multiplexer_56_out, multiplexer_57_out, multiplexer_58_out, multiplexer_59_out, multiplexer_60_out,
       multiplexer_61_out, multiplexer_62_out, multiplexer_65_out, multiplexer_66_out, multiplexer_67_out,
       multiplexer_68_out, multiplexer_69_out, multiplexer_70_out, multiplexer_71_out, multiplexer_72_out,
       multiplexer_75_out, multiplexer_76_out, multiplexer_77_out, multiplexer_78_out, multiplexer_79_out,
       multiplexer_80_out, multiplexer_81_out, multiplexer_82_out, multiplexer_85_out, multiplexer_86_out,
       multiplexer_87_out, multiplexer_88_out, multiplexer_89_out, multiplexer_90_out, multiplexer_91_out,
       multiplexer_92_out, multiplexer_95_out, multiplexer_96_out, multiplexer_97_out, multiplexer_98_out,
       multiplexer_99_out, multiplexer_100_out, multiplexer_101_out, multiplexer_102_out,
       multiplexer_105_out, multiplexer_106_out, multiplexer_107_out, multiplexer_108_out,
       multiplexer_109_out, multiplexer_110_out, multiplexer_111_out, multiplexer_112_out,
       multiplexer_115_out, multiplexer_116_out, multiplexer_117_out, multiplexer_118_out,
       multiplexer_119_out, multiplexer_120_out, multiplexer_121_out, multiplexer_122_out,
       multiplexer_125_out, multiplexer_126_out, multiplexer_127_out, multiplexer_128_out,
       multiplexer_129_out, multiplexer_130_out, multiplexer_131_out, multiplexer_132_out,
       multiplexer_135_out, multiplexer_136_out, multiplexer_137_out, multiplexer_138_out,
       multiplexer_139_out, multiplexer_140_out, multiplexer_141_out, multiplexer_142_out,
       multiplexer_145_out, multiplexer_146_out, multiplexer_147_out, multiplexer_148_out,
       multiplexer_149_out, multiplexer_150_out, multiplexer_151_out, multiplexer_152_out,
       multiplexer_155_out, multiplexer_156_out, multiplexer_157_out, multiplexer_158_out,
       multiplexer_159_out;

  Multiplexer multiplexer_1 (.in0(1'b0), .in1(Input[31]), .out(multiplexer_1_out), .sel(logi));
  Multiplexer multiplexer_2 (.in0(Input[31]), .in1(multiplexer_1_out), .out(multiplexer_2_out), .sel(Sa[4]));
  Multiplexer multiplexer_3 (.in0(multiplexer_2_out), .in1(multiplexer_1_out), .out(multiplexer_3_out), .sel(Sa[3]));
  Multiplexer multiplexer_4 (.in0(multiplexer_3_out), .in1(multiplexer_1_out), .out(multiplexer_4_out), .sel(Sa[2]));
  Multiplexer multiplexer_5 (.in0(Input[30]), .in1(multiplexer_1_out), .out(multiplexer_5_out), .sel(Sa[4]));
  Multiplexer multiplexer_6 (.in0(Input[29]), .in1(multiplexer_1_out), .out(multiplexer_6_out), .sel(Sa[4]));
  Multiplexer multiplexer_7 (.in0(multiplexer_5_out), .in1(multiplexer_1_out), .out(multiplexer_7_out), .sel(Sa[3]));
  Multiplexer multiplexer_8 (.in0(multiplexer_6_out), .in1(multiplexer_1_out), .out(multiplexer_8_out), .sel(Sa[3]));
  Multiplexer multiplexer_9 (.in0(multiplexer_7_out), .in1(multiplexer_1_out), .out(multiplexer_9_out), .sel(Sa[2]));
  Multiplexer multiplexer_10 (.in0(multiplexer_8_out), .in1(multiplexer_1_out), .out(multiplexer_10_out), .sel(Sa[2]));
  Multiplexer multiplexer_11 (.in0(multiplexer_4_out), .in1(multiplexer_1_out), .out(multiplexer_11_out), .sel(Sa[1]));
  Multiplexer multiplexer_12 (.in0(multiplexer_9_out), .in1(multiplexer_1_out), .out(multiplexer_12_out), .sel(Sa[1]));
  Multiplexer multiplexer_13 (.in0(multiplexer_11_out), .in1(multiplexer_1_out), .out(OUTPUT[31]), .sel(Sa[0]));
  Multiplexer multiplexer_14 (.in0(multiplexer_12_out), .in1(multiplexer_11_out), .out(OUTPUT[30]), .sel(Sa[0]));
  Multiplexer multiplexer_15 (.in0(Input[28]), .in1(multiplexer_1_out), .out(multiplexer_15_out), .sel(Sa[4]));
  Multiplexer multiplexer_16 (.in0(Input[27]), .in1(multiplexer_1_out), .out(multiplexer_16_out), .sel(Sa[4]));
  Multiplexer multiplexer_17 (.in0(multiplexer_15_out), .in1(multiplexer_1_out), .out(multiplexer_17_out), .sel(Sa[3]));
  Multiplexer multiplexer_18 (.in0(multiplexer_16_out), .in1(multiplexer_1_out), .out(multiplexer_18_out), .sel(Sa[3]));
  Multiplexer multiplexer_19 (.in0(multiplexer_17_out), .in1(multiplexer_1_out), .out(multiplexer_19_out), .sel(Sa[2]));
  Multiplexer multiplexer_20 (.in0(multiplexer_18_out), .in1(multiplexer_3_out), .out(multiplexer_20_out), .sel(Sa[2]));
  Multiplexer multiplexer_21 (.in0(multiplexer_10_out), .in1(multiplexer_4_out), .out(multiplexer_21_out), .sel(Sa[1]));
  Multiplexer multiplexer_22 (.in0(multiplexer_19_out), .in1(multiplexer_9_out), .out(multiplexer_22_out), .sel(Sa[1]));
  Multiplexer multiplexer_23 (.in0(multiplexer_21_out), .in1(multiplexer_12_out), .out(OUTPUT[29]), .sel(Sa[0]));
  Multiplexer multiplexer_24 (.in0(multiplexer_22_out), .in1(multiplexer_21_out), .out(OUTPUT[28]), .sel(Sa[0]));
  Multiplexer multiplexer_25 (.in0(Input[26]), .in1(multiplexer_1_out), .out(multiplexer_25_out), .sel(Sa[4]));
  Multiplexer multiplexer_26 (.in0(Input[25]), .in1(multiplexer_1_out), .out(multiplexer_26_out), .sel(Sa[4]));
  Multiplexer multiplexer_27 (.in0(multiplexer_25_out), .in1(multiplexer_1_out), .out(multiplexer_27_out), .sel(Sa[3]));
  Multiplexer multiplexer_28 (.in0(multiplexer_26_out), .in1(multiplexer_1_out), .out(multiplexer_28_out), .sel(Sa[3]));
  Multiplexer multiplexer_29 (.in0(multiplexer_27_out), .in1(multiplexer_7_out), .out(multiplexer_29_out), .sel(Sa[2]));
  Multiplexer multiplexer_30 (.in0(multiplexer_28_out), .in1(multiplexer_8_out), .out(multiplexer_30_out), .sel(Sa[2]));
  Multiplexer multiplexer_31 (
    .in0(multiplexer_20_out), .in1(multiplexer_10_out), .out(multiplexer_31_out), .sel(Sa[1]));
  Multiplexer multiplexer_32 (
    .in0(multiplexer_29_out), .in1(multiplexer_19_out), .out(multiplexer_32_out), .sel(Sa[1]));
  Multiplexer multiplexer_33 (.in0(multiplexer_31_out), .in1(multiplexer_22_out), .out(OUTPUT[27]), .sel(Sa[0]));
  Multiplexer multiplexer_34 (.in0(multiplexer_32_out), .in1(multiplexer_31_out), .out(OUTPUT[26]), .sel(Sa[0]));
  Multiplexer multiplexer_35 (.in0(Input[24]), .in1(multiplexer_1_out), .out(multiplexer_35_out), .sel(Sa[4]));
  Multiplexer multiplexer_36 (.in0(Input[23]), .in1(multiplexer_1_out), .out(multiplexer_36_out), .sel(Sa[4]));
  Multiplexer multiplexer_37 (.in0(multiplexer_35_out), .in1(multiplexer_1_out), .out(multiplexer_37_out), .sel(Sa[3]));
  Multiplexer multiplexer_38 (.in0(multiplexer_36_out), .in1(multiplexer_2_out), .out(multiplexer_38_out), .sel(Sa[3]));
  Multiplexer multiplexer_39 (
    .in0(multiplexer_37_out), .in1(multiplexer_17_out), .out(multiplexer_39_out), .sel(Sa[2]));
  Multiplexer multiplexer_40 (
    .in0(multiplexer_38_out), .in1(multiplexer_18_out), .out(multiplexer_40_out), .sel(Sa[2]));
  Multiplexer multiplexer_41 (
    .in0(multiplexer_30_out), .in1(multiplexer_20_out), .out(multiplexer_41_out), .sel(Sa[1]));
  Multiplexer multiplexer_42 (
    .in0(multiplexer_39_out), .in1(multiplexer_29_out), .out(multiplexer_42_out), .sel(Sa[1]));
  Multiplexer multiplexer_43 (.in0(multiplexer_41_out), .in1(multiplexer_32_out), .out(OUTPUT[25]), .sel(Sa[0]));
  Multiplexer multiplexer_44 (.in0(multiplexer_42_out), .in1(multiplexer_41_out), .out(OUTPUT[24]), .sel(Sa[0]));
  Multiplexer multiplexer_45 (.in0(Input[21]), .in1(multiplexer_1_out), .out(multiplexer_45_out), .sel(Sa[4]));
  Multiplexer multiplexer_46 (.in0(Input[22]), .in1(multiplexer_1_out), .out(multiplexer_46_out), .sel(Sa[4]));
  Multiplexer multiplexer_47 (.in0(multiplexer_45_out), .in1(multiplexer_6_out), .out(multiplexer_47_out), .sel(Sa[3]));
  Multiplexer multiplexer_48 (.in0(multiplexer_46_out), .in1(multiplexer_5_out), .out(multiplexer_48_out), .sel(Sa[3]));
  Multiplexer multiplexer_49 (
    .in0(multiplexer_47_out), .in1(multiplexer_28_out), .out(multiplexer_49_out), .sel(Sa[2]));
  Multiplexer multiplexer_50 (
    .in0(multiplexer_48_out), .in1(multiplexer_27_out), .out(multiplexer_50_out), .sel(Sa[2]));
  Multiplexer multiplexer_51 (
    .in0(multiplexer_50_out), .in1(multiplexer_39_out), .out(multiplexer_51_out), .sel(Sa[1]));
  Multiplexer multiplexer_52 (
    .in0(multiplexer_40_out), .in1(multiplexer_30_out), .out(multiplexer_52_out), .sel(Sa[1]));
  Multiplexer multiplexer_53 (.in0(multiplexer_51_out), .in1(multiplexer_52_out), .out(OUTPUT[22]), .sel(Sa[0]));
  Multiplexer multiplexer_54 (.in0(multiplexer_52_out), .in1(multiplexer_42_out), .out(OUTPUT[23]), .sel(Sa[0]));
  Multiplexer multiplexer_55 (.in0(Input[20]), .in1(multiplexer_1_out), .out(multiplexer_55_out), .sel(Sa[4]));
  Multiplexer multiplexer_56 (.in0(Input[19]), .in1(multiplexer_1_out), .out(multiplexer_56_out), .sel(Sa[4]));
  Multiplexer multiplexer_57 (
    .in0(multiplexer_55_out), .in1(multiplexer_15_out), .out(multiplexer_57_out), .sel(Sa[3]));
  Multiplexer multiplexer_58 (
    .in0(multiplexer_56_out), .in1(multiplexer_16_out), .out(multiplexer_58_out), .sel(Sa[3]));
  Multiplexer multiplexer_59 (
    .in0(multiplexer_57_out), .in1(multiplexer_37_out), .out(multiplexer_59_out), .sel(Sa[2]));
  Multiplexer multiplexer_60 (
    .in0(multiplexer_58_out), .in1(multiplexer_38_out), .out(multiplexer_60_out), .sel(Sa[2]));
  Multiplexer multiplexer_61 (
    .in0(multiplexer_49_out), .in1(multiplexer_40_out), .out(multiplexer_61_out), .sel(Sa[1]));
  Multiplexer multiplexer_62 (
    .in0(multiplexer_59_out), .in1(multiplexer_50_out), .out(multiplexer_62_out), .sel(Sa[1]));
  Multiplexer multiplexer_63 (.in0(multiplexer_61_out), .in1(multiplexer_51_out), .out(OUTPUT[21]), .sel(Sa[0]));
  Multiplexer multiplexer_64 (.in0(multiplexer_62_out), .in1(multiplexer_61_out), .out(OUTPUT[20]), .sel(Sa[0]));
  Multiplexer multiplexer_65 (.in0(Input[18]), .in1(multiplexer_1_out), .out(multiplexer_65_out), .sel(Sa[4]));
  Multiplexer multiplexer_66 (.in0(Input[17]), .in1(multiplexer_1_out), .out(multiplexer_66_out), .sel(Sa[4]));
  Multiplexer multiplexer_67 (
    .in0(multiplexer_65_out), .in1(multiplexer_25_out), .out(multiplexer_67_out), .sel(Sa[3]));
  Multiplexer multiplexer_68 (
    .in0(multiplexer_66_out), .in1(multiplexer_26_out), .out(multiplexer_68_out), .sel(Sa[3]));
  Multiplexer multiplexer_69 (
    .in0(multiplexer_67_out), .in1(multiplexer_48_out), .out(multiplexer_69_out), .sel(Sa[2]));
  Multiplexer multiplexer_70 (
    .in0(multiplexer_68_out), .in1(multiplexer_47_out), .out(multiplexer_70_out), .sel(Sa[2]));
  Multiplexer multiplexer_71 (
    .in0(multiplexer_60_out), .in1(multiplexer_49_out), .out(multiplexer_71_out), .sel(Sa[1]));
  Multiplexer multiplexer_72 (
    .in0(multiplexer_69_out), .in1(multiplexer_59_out), .out(multiplexer_72_out), .sel(Sa[1]));
  Multiplexer multiplexer_73 (.in0(multiplexer_71_out), .in1(multiplexer_62_out), .out(OUTPUT[19]), .sel(Sa[0]));
  Multiplexer multiplexer_74 (.in0(multiplexer_72_out), .in1(multiplexer_71_out), .out(OUTPUT[18]), .sel(Sa[0]));
  Multiplexer multiplexer_75 (.in0(Input[16]), .in1(multiplexer_1_out), .out(multiplexer_75_out), .sel(Sa[4]));
  Multiplexer multiplexer_76 (.in0(Input[15]), .in1(Input[31]), .out(multiplexer_76_out), .sel(Sa[4]));
  Multiplexer multiplexer_77 (
    .in0(multiplexer_75_out), .in1(multiplexer_35_out), .out(multiplexer_77_out), .sel(Sa[3]));
  Multiplexer multiplexer_78 (
    .in0(multiplexer_76_out), .in1(multiplexer_36_out), .out(multiplexer_78_out), .sel(Sa[3]));
  Multiplexer multiplexer_79 (
    .in0(multiplexer_77_out), .in1(multiplexer_57_out), .out(multiplexer_79_out), .sel(Sa[2]));
  Multiplexer multiplexer_80 (
    .in0(multiplexer_78_out), .in1(multiplexer_58_out), .out(multiplexer_80_out), .sel(Sa[2]));
  Multiplexer multiplexer_81 (
    .in0(multiplexer_70_out), .in1(multiplexer_60_out), .out(multiplexer_81_out), .sel(Sa[1]));
  Multiplexer multiplexer_82 (
    .in0(multiplexer_79_out), .in1(multiplexer_69_out), .out(multiplexer_82_out), .sel(Sa[1]));
  Multiplexer multiplexer_83 (.in0(multiplexer_81_out), .in1(multiplexer_72_out), .out(OUTPUT[17]), .sel(Sa[0]));
  Multiplexer multiplexer_84 (.in0(multiplexer_82_out), .in1(multiplexer_81_out), .out(OUTPUT[16]), .sel(Sa[0]));
  Multiplexer multiplexer_85 (.in0(Input[14]), .in1(Input[30]), .out(multiplexer_85_out), .sel(Sa[4]));
  Multiplexer multiplexer_86 (.in0(Input[13]), .in1(Input[29]), .out(multiplexer_86_out), .sel(Sa[4]));
  Multiplexer multiplexer_87 (
    .in0(multiplexer_85_out), .in1(multiplexer_46_out), .out(multiplexer_87_out), .sel(Sa[3]));
  Multiplexer multiplexer_88 (
    .in0(multiplexer_86_out), .in1(multiplexer_45_out), .out(multiplexer_88_out), .sel(Sa[3]));
  Multiplexer multiplexer_89 (
    .in0(multiplexer_87_out), .in1(multiplexer_67_out), .out(multiplexer_89_out), .sel(Sa[2]));
  Multiplexer multiplexer_90 (
    .in0(multiplexer_88_out), .in1(multiplexer_68_out), .out(multiplexer_90_out), .sel(Sa[2]));
  Multiplexer multiplexer_91 (
    .in0(multiplexer_80_out), .in1(multiplexer_70_out), .out(multiplexer_91_out), .sel(Sa[1]));
  Multiplexer multiplexer_92 (
    .in0(multiplexer_89_out), .in1(multiplexer_79_out), .out(multiplexer_92_out), .sel(Sa[1]));
  Multiplexer multiplexer_93 (.in0(multiplexer_91_out), .in1(multiplexer_82_out), .out(OUTPUT[15]), .sel(Sa[0]));
  Multiplexer multiplexer_94 (.in0(multiplexer_92_out), .in1(multiplexer_91_out), .out(OUTPUT[14]), .sel(Sa[0]));
  Multiplexer multiplexer_95 (.in0(Input[12]), .in1(Input[28]), .out(multiplexer_95_out), .sel(Sa[4]));
  Multiplexer multiplexer_96 (.in0(Input[11]), .in1(Input[27]), .out(multiplexer_96_out), .sel(Sa[4]));
  Multiplexer multiplexer_97 (
    .in0(multiplexer_95_out), .in1(multiplexer_55_out), .out(multiplexer_97_out), .sel(Sa[3]));
  Multiplexer multiplexer_98 (
    .in0(multiplexer_96_out), .in1(multiplexer_56_out), .out(multiplexer_98_out), .sel(Sa[3]));
  Multiplexer multiplexer_99 (
    .in0(multiplexer_97_out), .in1(multiplexer_77_out), .out(multiplexer_99_out), .sel(Sa[2]));
  Multiplexer multiplexer_100 (
    .in0(multiplexer_98_out), .in1(multiplexer_78_out), .out(multiplexer_100_out), .sel(Sa[2]));
  Multiplexer multiplexer_101 (
    .in0(multiplexer_90_out), .in1(multiplexer_80_out), .out(multiplexer_101_out), .sel(Sa[1]));
  Multiplexer multiplexer_102 (
    .in0(multiplexer_99_out), .in1(multiplexer_89_out), .out(multiplexer_102_out), .sel(Sa[1]));
  Multiplexer multiplexer_103 (.in0(multiplexer_101_out), .in1(multiplexer_92_out), .out(OUTPUT[13]), .sel(Sa[0]));
  Multiplexer multiplexer_104 (.in0(multiplexer_102_out), .in1(multiplexer_101_out), .out(OUTPUT[12]), .sel(Sa[0]));
  Multiplexer multiplexer_105 (.in0(Input[10]), .in1(Input[26]), .out(multiplexer_105_out), .sel(Sa[4]));
  Multiplexer multiplexer_106 (.in0(Input[9]), .in1(Input[25]), .out(multiplexer_106_out), .sel(Sa[4]));
  Multiplexer multiplexer_107 (
    .in0(multiplexer_105_out), .in1(multiplexer_65_out), .out(multiplexer_107_out), .sel(Sa[3]));
  Multiplexer multiplexer_108 (
    .in0(multiplexer_106_out), .in1(multiplexer_66_out), .out(multiplexer_108_out), .sel(Sa[3]));
  Multiplexer multiplexer_109 (
    .in0(multiplexer_107_out), .in1(multiplexer_87_out), .out(multiplexer_109_out), .sel(Sa[2]));
  Multiplexer multiplexer_110 (
    .in0(multiplexer_108_out), .in1(multiplexer_88_out), .out(multiplexer_110_out), .sel(Sa[2]));
  Multiplexer multiplexer_111 (
    .in0(multiplexer_100_out), .in1(multiplexer_90_out), .out(multiplexer_111_out), .sel(Sa[1]));
  Multiplexer multiplexer_112 (
    .in0(multiplexer_109_out), .in1(multiplexer_99_out), .out(multiplexer_112_out), .sel(Sa[1]));
  Multiplexer multiplexer_113 (.in0(multiplexer_111_out), .in1(multiplexer_102_out), .out(OUTPUT[11]), .sel(Sa[0]));
  Multiplexer multiplexer_114 (.in0(multiplexer_112_out), .in1(multiplexer_111_out), .out(OUTPUT[10]), .sel(Sa[0]));
  Multiplexer multiplexer_115 (.in0(Input[8]), .in1(Input[24]), .out(multiplexer_115_out), .sel(Sa[4]));
  Multiplexer multiplexer_116 (.in0(Input[7]), .in1(Input[23]), .out(multiplexer_116_out), .sel(Sa[4]));
  Multiplexer multiplexer_117 (
    .in0(multiplexer_115_out), .in1(multiplexer_75_out), .out(multiplexer_117_out), .sel(Sa[3]));
  Multiplexer multiplexer_118 (
    .in0(multiplexer_116_out), .in1(multiplexer_76_out), .out(multiplexer_118_out), .sel(Sa[3]));
  Multiplexer multiplexer_119 (
    .in0(multiplexer_117_out), .in1(multiplexer_97_out), .out(multiplexer_119_out), .sel(Sa[2]));
  Multiplexer multiplexer_120 (
    .in0(multiplexer_118_out), .in1(multiplexer_98_out), .out(multiplexer_120_out), .sel(Sa[2]));
  Multiplexer multiplexer_121 (
    .in0(multiplexer_110_out), .in1(multiplexer_100_out), .out(multiplexer_121_out), .sel(Sa[1]));
  Multiplexer multiplexer_122 (
    .in0(multiplexer_119_out), .in1(multiplexer_109_out), .out(multiplexer_122_out), .sel(Sa[1]));
  Multiplexer multiplexer_123 (.in0(multiplexer_121_out), .in1(multiplexer_112_out), .out(OUTPUT[9]), .sel(Sa[0]));
  Multiplexer multiplexer_124 (.in0(multiplexer_122_out), .in1(multiplexer_121_out), .out(OUTPUT[8]), .sel(Sa[0]));
  Multiplexer multiplexer_125 (.in0(Input[6]), .in1(Input[22]), .out(multiplexer_125_out), .sel(Sa[4]));
  Multiplexer multiplexer_126 (.in0(Input[5]), .in1(Input[21]), .out(multiplexer_126_out), .sel(Sa[4]));
  Multiplexer multiplexer_127 (
    .in0(multiplexer_125_out), .in1(multiplexer_85_out), .out(multiplexer_127_out), .sel(Sa[3]));
  Multiplexer multiplexer_128 (
    .in0(multiplexer_126_out), .in1(multiplexer_86_out), .out(multiplexer_128_out), .sel(Sa[3]));
  Multiplexer multiplexer_129 (
    .in0(multiplexer_127_out), .in1(multiplexer_107_out), .out(multiplexer_129_out), .sel(Sa[2]));
  Multiplexer multiplexer_130 (
    .in0(multiplexer_128_out), .in1(multiplexer_108_out), .out(multiplexer_130_out), .sel(Sa[2]));
  Multiplexer multiplexer_131 (
    .in0(multiplexer_120_out), .in1(multiplexer_110_out), .out(multiplexer_131_out), .sel(Sa[1]));
  Multiplexer multiplexer_132 (
    .in0(multiplexer_129_out), .in1(multiplexer_119_out), .out(multiplexer_132_out), .sel(Sa[1]));
  Multiplexer multiplexer_133 (.in0(multiplexer_131_out), .in1(multiplexer_122_out), .out(OUTPUT[7]), .sel(Sa[0]));
  Multiplexer multiplexer_134 (.in0(multiplexer_132_out), .in1(multiplexer_131_out), .out(OUTPUT[6]), .sel(Sa[0]));
  Multiplexer multiplexer_135 (.in0(Input[4]), .in1(Input[20]), .out(multiplexer_135_out), .sel(Sa[4]));
  Multiplexer multiplexer_136 (.in0(Input[3]), .in1(Input[19]), .out(multiplexer_136_out), .sel(Sa[4]));
  Multiplexer multiplexer_137 (
    .in0(multiplexer_135_out), .in1(multiplexer_95_out), .out(multiplexer_137_out), .sel(Sa[3]));
  Multiplexer multiplexer_138 (
    .in0(multiplexer_136_out), .in1(multiplexer_96_out), .out(multiplexer_138_out), .sel(Sa[3]));
  Multiplexer multiplexer_139 (
    .in0(multiplexer_137_out), .in1(multiplexer_117_out), .out(multiplexer_139_out), .sel(Sa[2]));
  Multiplexer multiplexer_140 (
    .in0(multiplexer_138_out), .in1(multiplexer_118_out), .out(multiplexer_140_out), .sel(Sa[2]));
  Multiplexer multiplexer_141 (
    .in0(multiplexer_130_out), .in1(multiplexer_120_out), .out(multiplexer_141_out), .sel(Sa[1]));
  Multiplexer multiplexer_142 (
    .in0(multiplexer_139_out), .in1(multiplexer_129_out), .out(multiplexer_142_out), .sel(Sa[1]));
  Multiplexer multiplexer_143 (.in0(multiplexer_141_out), .in1(multiplexer_132_out), .out(OUTPUT[5]), .sel(Sa[0]));
  Multiplexer multiplexer_144 (.in0(multiplexer_142_out), .in1(multiplexer_141_out), .out(OUTPUT[4]), .sel(Sa[0]));
  Multiplexer multiplexer_145 (.in0(Input[2]), .in1(Input[18]), .out(multiplexer_145_out), .sel(Sa[4]));
  Multiplexer multiplexer_146 (.in0(Input[1]), .in1(Input[17]), .out(multiplexer_146_out), .sel(Sa[4]));
  Multiplexer multiplexer_147 (
    .in0(multiplexer_145_out), .in1(multiplexer_105_out), .out(multiplexer_147_out), .sel(Sa[3]));
  Multiplexer multiplexer_148 (
    .in0(multiplexer_146_out), .in1(multiplexer_106_out), .out(multiplexer_148_out), .sel(Sa[3]));
  Multiplexer multiplexer_149 (
    .in0(multiplexer_147_out), .in1(multiplexer_127_out), .out(multiplexer_149_out), .sel(Sa[2]));
  Multiplexer multiplexer_150 (
    .in0(multiplexer_148_out), .in1(multiplexer_128_out), .out(multiplexer_150_out), .sel(Sa[2]));
  Multiplexer multiplexer_151 (
    .in0(multiplexer_140_out), .in1(multiplexer_130_out), .out(multiplexer_151_out), .sel(Sa[1]));
  Multiplexer multiplexer_152 (
    .in0(multiplexer_149_out), .in1(multiplexer_139_out), .out(multiplexer_152_out), .sel(Sa[1]));
  Multiplexer multiplexer_153 (.in0(multiplexer_151_out), .in1(multiplexer_142_out), .out(OUTPUT[3]), .sel(Sa[0]));
  Multiplexer multiplexer_154 (.in0(multiplexer_152_out), .in1(multiplexer_151_out), .out(OUTPUT[2]), .sel(Sa[0]));
  Multiplexer multiplexer_155 (.in0(Input[0]), .in1(Input[16]), .out(multiplexer_155_out), .sel(Sa[4]));
  Multiplexer multiplexer_156 (
    .in0(multiplexer_155_out), .in1(multiplexer_115_out), .out(multiplexer_156_out), .sel(Sa[3]));
  Multiplexer multiplexer_157 (
    .in0(multiplexer_156_out), .in1(multiplexer_137_out), .out(multiplexer_157_out), .sel(Sa[2]));
  Multiplexer multiplexer_158 (
    .in0(multiplexer_150_out), .in1(multiplexer_140_out), .out(multiplexer_158_out), .sel(Sa[1]));
  Multiplexer multiplexer_159 (
    .in0(multiplexer_157_out), .in1(multiplexer_149_out), .out(multiplexer_159_out), .sel(Sa[1]));
  Multiplexer multiplexer_160 (.in0(multiplexer_158_out), .in1(multiplexer_152_out), .out(OUTPUT[1]), .sel(Sa[0]));
  Multiplexer multiplexer_161 (.in0(multiplexer_159_out), .in1(multiplexer_158_out), .out(OUTPUT[0]), .sel(Sa[0]));
endmodule

module OR (
  input  [31:0] A,
  input  [31:0] B,
  output [31:0] C
);

  or or_1 (C[0], A[0], B[0]);
  or or_2 (C[1], A[1], B[1]);
  or or_3 (C[2], A[2], B[2]);
  or or_4 (C[3], A[3], B[3]);
  or or_5 (C[4], A[4], B[4]);
  or or_6 (C[5], A[5], B[5]);
  or or_7 (C[6], A[6], B[6]);
  or or_8 (C[7], A[7], B[7]);
  or or_9 (C[8], A[8], B[8]);
  or or_10 (C[9], A[9], B[9]);
  or or_11 (C[10], A[10], B[10]);
  or or_12 (C[11], A[11], B[11]);
  or or_13 (C[12], A[12], B[12]);
  or or_14 (C[13], A[13], B[13]);
  or or_15 (C[14], A[14], B[14]);
  or or_16 (C[15], A[15], B[15]);
  or or_17 (C[16], A[16], B[16]);
  or or_18 (C[17], A[17], B[17]);
  or or_19 (C[18], A[18], B[18]);
  or or_20 (C[19], A[19], B[19]);
  or or_21 (C[20], A[20], B[20]);
  or or_22 (C[21], A[21], B[21]);
  or or_23 (C[22], A[22], B[22]);
  or or_24 (C[23], A[23], B[23]);
  or or_25 (C[24], A[24], B[24]);
  or or_26 (C[25], A[25], B[25]);
  or or_27 (C[26], A[26], B[26]);
  or or_28 (C[27], A[27], B[27]);
  or or_29 (C[28], A[28], B[28]);
  or or_30 (C[29], A[29], B[29]);
  or or_31 (C[30], A[30], B[30]);
  or or_32 (C[31], A[31], B[31]);
endmodule

module NOT (
  input  [31:0] A,
  output [31:0] B
);

  not not_1 (B[0], A[0]);
  not not_2 (B[1], A[1]);
  not not_3 (B[2], A[2]);
  not not_4 (B[3], A[3]);
  not not_5 (B[4], A[4]);
  not not_6 (B[5], A[5]);
  not not_7 (B[6], A[6]);
  not not_8 (B[7], A[7]);
  not not_9 (B[8], A[8]);
  not not_10 (B[9], A[9]);
  not not_11 (B[10], A[10]);
  not not_12 (B[11], A[11]);
  not not_13 (B[12], A[12]);
  not not_14 (B[13], A[13]);
  not not_15 (B[14], A[14]);
  not not_16 (B[15], A[15]);
  not not_17 (B[16], A[16]);
  not not_18 (B[17], A[17]);
  not not_19 (B[18], A[18]);
  not not_20 (B[19], A[19]);
  not not_21 (B[20], A[20]);
  not not_22 (B[21], A[21]);
  not not_23 (B[22], A[22]);
  not not_24 (B[23], A[23]);
  not not_25 (B[24], A[24]);
  not not_26 (B[25], A[25]);
  not not_27 (B[26], A[26]);
  not not_28 (B[27], A[27]);
  not not_29 (B[28], A[28]);
  not not_30 (B[29], A[29]);
  not not_31 (B[30], A[30]);
  not not_32 (B[31], A[31]);
endmodule

module XOR (
  input  [31:0] A,
  input  [31:0] B,
  output [31:0] C
);

  xor xor_1 (C[0], A[0], B[0]);
  xor xor_2 (C[1], A[1], B[1]);
  xor xor_3 (C[2], A[2], B[2]);
  xor xor_4 (C[3], A[3], B[3]);
  xor xor_5 (C[4], A[4], B[4]);
  xor xor_6 (C[5], A[5], B[5]);
  xor xor_7 (C[6], A[6], B[6]);
  xor xor_8 (C[7], A[7], B[7]);
  xor xor_9 (C[8], A[8], B[8]);
  xor xor_10 (C[9], A[9], B[9]);
  xor xor_11 (C[10], A[10], B[10]);
  xor xor_12 (C[11], A[11], B[11]);
  xor xor_13 (C[12], A[12], B[12]);
  xor xor_14 (C[13], A[13], B[13]);
  xor xor_15 (C[14], A[14], B[14]);
  xor xor_16 (C[15], A[15], B[15]);
  xor xor_17 (C[16], A[16], B[16]);
  xor xor_18 (C[17], A[17], B[17]);
  xor xor_19 (C[18], A[18], B[18]);
  xor xor_20 (C[19], A[19], B[19]);
  xor xor_21 (C[20], A[20], B[20]);
  xor xor_22 (C[21], A[21], B[21]);
  xor xor_23 (C[22], A[22], B[22]);
  xor xor_24 (C[23], A[23], B[23]);
  xor xor_25 (C[24], A[24], B[24]);
  xor xor_26 (C[25], A[25], B[25]);
  xor xor_27 (C[26], A[26], B[26]);
  xor xor_28 (C[27], A[27], B[27]);
  xor xor_29 (C[28], A[28], B[28]);
  xor xor_30 (C[29], A[29], B[29]);
  xor xor_31 (C[30], A[30], B[30]);
  xor xor_32 (C[31], A[31], B[31]);
endmodule

module AND (
  input  [31:0] A,
  input  [31:0] B,
  output [31:0] C
);

  and and_1 (C[0], A[0], B[0]);
  and and_2 (C[1], A[1], B[1]);
  and and_3 (C[2], A[2], B[2]);
  and and_4 (C[3], A[3], B[3]);
  and and_5 (C[4], A[4], B[4]);
  and and_6 (C[5], A[5], B[5]);
  and and_7 (C[6], A[6], B[6]);
  and and_8 (C[7], A[7], B[7]);
  and and_9 (C[8], A[8], B[8]);
  and and_10 (C[9], A[9], B[9]);
  and and_11 (C[10], A[10], B[10]);
  and and_12 (C[11], A[11], B[11]);
  and and_13 (C[12], A[12], B[12]);
  and and_14 (C[13], A[13], B[13]);
  and and_15 (C[14], A[14], B[14]);
  and and_16 (C[15], A[15], B[15]);
  and and_17 (C[16], A[16], B[16]);
  and and_18 (C[17], A[17], B[17]);
  and and_19 (C[18], A[18], B[18]);
  and and_20 (C[19], A[19], B[19]);
  and and_21 (C[20], A[20], B[20]);
  and and_22 (C[21], A[21], B[21]);
  and and_23 (C[22], A[22], B[22]);
  and and_24 (C[23], A[23], B[23]);
  and and_25 (C[24], A[24], B[24]);
  and and_26 (C[25], A[25], B[25]);
  and and_27 (C[26], A[26], B[26]);
  and and_28 (C[27], A[27], B[27]);
  and and_29 (C[28], A[28], B[28]);
  and and_30 (C[29], A[29], B[29]);
  and and_31 (C[30], A[30], B[30]);
  and and_32 (C[31], A[31], B[31]);
endmodule

module NOR (
  input  [31:0] A,
  input  [31:0] B,
  output [31:0] C
);

  nor nor_1 (C[0], A[0], B[0]);
  nor nor_2 (C[1], A[1], B[1]);
  nor nor_3 (C[2], A[2], B[2]);
  nor nor_4 (C[3], A[3], B[3]);
  nor nor_5 (C[4], A[4], B[4]);
  nor nor_6 (C[5], A[5], B[5]);
  nor nor_7 (C[6], A[6], B[6]);
  nor nor_8 (C[7], A[7], B[7]);
  nor nor_9 (C[8], A[8], B[8]);
  nor nor_10 (C[9], A[9], B[9]);
  nor nor_11 (C[10], A[10], B[10]);
  nor nor_12 (C[11], A[11], B[11]);
  nor nor_13 (C[12], A[12], B[12]);
  nor nor_14 (C[13], A[13], B[13]);
  nor nor_15 (C[14], A[14], B[14]);
  nor nor_16 (C[15], A[15], B[15]);
  nor nor_17 (C[16], A[16], B[16]);
  nor nor_18 (C[17], A[17], B[17]);
  nor nor_19 (C[18], A[18], B[18]);
  nor nor_20 (C[19], A[19], B[19]);
  nor nor_21 (C[20], A[20], B[20]);
  nor nor_22 (C[21], A[21], B[21]);
  nor nor_23 (C[22], A[22], B[22]);
  nor nor_24 (C[23], A[23], B[23]);
  nor nor_25 (C[24], A[24], B[24]);
  nor nor_26 (C[25], A[25], B[25]);
  nor nor_27 (C[26], A[26], B[26]);
  nor nor_28 (C[27], A[27], B[27]);
  nor nor_29 (C[28], A[28], B[28]);
  nor nor_30 (C[29], A[29], B[29]);
  nor nor_31 (C[30], A[30], B[30]);
  nor nor_32 (C[31], A[31], B[31]);
endmodule

module Div4 (
  input  [3:0] in_1,
  input  [3:0] in_2,
  output [3:0] out_3,
  output [3:0] out_4
);

  wire comparator_1_gt, comparator_2_gt, comparator_3_gt, comparator_4_gt;
  wire [3:0] multiplexer_1_out, multiplexer_2_out, multiplexer_3_out, multiplexer_4_out, multiplexer_5_out,
       multiplexer_6_out, or_1_out, or_2_out, or_3_out, or_4_out, subtractor_1_out, subtractor_2_out,
       subtractor_3_out, subtractor_4_out;
  wire [7:0] shifter_1_out, shifter_2_out, shifter_3_out, shifter_4_out;

  assign or_1_out = 4'b0001 | shifter_1_out[3:0];  // OR_Gate or_1, 4 bits wide
  Shifter shifter_1 (.in({4'b0000, in_1}), .\dist (3'b001), .out(shifter_1_out));
  Multiplexer #(.disabled("Z"), .width(4)) multiplexer_1 (
    .in0(or_1_out), .in1(shifter_1_out[3:0]), .out(multiplexer_1_out), .sel(comparator_1_gt));
  Comparator #(.mode("unsigned"), .width(4)) comparator_1 (
    .a(in_2), .b(shifter_1_out[7:4]), .gt(comparator_1_gt));  // open: eq, lt
  Subtractor #(.width(4)) subtractor_1 (.a(shifter_1_out[7:4]), .b(in_2), .out(subtractor_1_out));  // open: bin, bout
  Multiplexer #(.disabled("Z"), .width(4)) multiplexer_2 (
    .in0(subtractor_1_out), .in1(shifter_1_out[7:4]), .out(multiplexer_2_out), .sel(comparator_1_gt));
  assign or_2_out = 4'b0001 | shifter_2_out[3:0];  // OR_Gate or_2, 4 bits wide
  Shifter shifter_2 (.in({multiplexer_2_out, multiplexer_1_out}), .\dist (3'b001), .out(shifter_2_out));
  Subtractor #(.width(4)) subtractor_2 (.a(shifter_2_out[7:4]), .b(in_2), .out(subtractor_2_out));  // open: bin, bout
  Multiplexer #(.disabled("Z"), .width(4)) multiplexer_3 (
    .in0(or_2_out), .in1(shifter_2_out[3:0]), .out(multiplexer_3_out), .sel(comparator_2_gt));
  Comparator #(.mode("unsigned"), .width(4)) comparator_2 (
    .a(in_2), .b(shifter_2_out[7:4]), .gt(comparator_2_gt));  // open: eq, lt
  Multiplexer #(.disabled("Z"), .width(4)) multiplexer_4 (
    .in0(subtractor_2_out), .in1(shifter_2_out[7:4]), .out(multiplexer_4_out), .sel(comparator_2_gt));
  assign or_3_out = 4'b0001 | shifter_3_out[3:0];  // OR_Gate or_3, 4 bits wide
  Shifter shifter_3 (.in({multiplexer_4_out, multiplexer_3_out}), .\dist (3'b001), .out(shifter_3_out));
  Multiplexer #(.disabled("Z"), .width(4)) multiplexer_5 (
    .in0(or_3_out), .in1(shifter_3_out[3:0]), .out(multiplexer_5_out), .sel(comparator_3_gt));
  Comparator #(.mode("unsigned"), .width(4)) comparator_3 (
    .a(in_2), .b(shifter_3_out[7:4]), .gt(comparator_3_gt));  // open: eq, lt
  Subtractor #(.width(4)) subtractor_3 (.a(shifter_3_out[7:4]), .b(in_2), .out(subtractor_3_out));  // open: bin, bout
  Multiplexer #(.disabled("Z"), .width(4)) multiplexer_6 (
    .in0(subtractor_3_out), .in1(shifter_3_out[7:4]), .out(multiplexer_6_out), .sel(comparator_3_gt));
  assign or_4_out = 4'b0001 | shifter_4_out[3:0];  // OR_Gate or_4, 4 bits wide
  Shifter shifter_4 (.in({multiplexer_6_out, multiplexer_5_out}), .\dist (3'b001), .out(shifter_4_out));
  Multiplexer #(.disabled("Z"), .width(4)) multiplexer_7 (
    .in0(or_4_out), .in1(shifter_4_out[3:0]), .out(out_3), .sel(comparator_4_gt));
  Comparator #(.mode("unsigned"), .width(4)) comparator_4 (
    .a(in_2), .b(shifter_4_out[7:4]), .gt(comparator_4_gt));  // open: eq, lt
  Subtractor #(.width(4)) subtractor_4 (.a(shifter_4_out[7:4]), .b(in_2), .out(subtractor_4_out));  // open: bin, bout
  Multiplexer #(.disabled("Z"), .width(4)) multiplexer_8 (
    .in0(subtractor_4_out), .in1(shifter_4_out[7:4]), .out(out_4), .sel(comparator_4_gt));
endmodule

module L_32_div1_c33d2353 (
  input  [31:0] in_1,
  input  [31:0] in_2,
  input  [31:0] in_3,
  output [31:0] out_4,
  output [31:0] out_5
);

  wire comparator_1_gt;
  wire [31:0] or_1_out, or_2_out, shifter_1_out, shifter_2_out, shifter_3_out, subtractor_1_out;

  Shifter #(.width(32)) shifter_1 (.in(in_2), .\dist (5'b00001), .out(shifter_1_out));
  Shifter #(.shift("lr"), .width(32)) shifter_2 (.in(in_3), .\dist ({5{1'b1}}), .out(shifter_2_out));
  assign or_1_out = shifter_1_out | shifter_2_out;  // OR_Gate or_1, 32 bits wide
  Shifter #(.width(32)) shifter_3 (.in(in_3), .\dist (5'b00001), .out(shifter_3_out));
  Subtractor #(.width(32)) subtractor_1 (.a(or_1_out), .b(in_1), .out(subtractor_1_out));  // open: bin, bout
  Multiplexer #(.disabled("Z"), .width(32)) multiplexer_1 (
    .in0(or_2_out), .in1(shifter_3_out), .out(out_5), .sel(comparator_1_gt));
  Comparator #(.mode("unsigned"), .width(32)) comparator_1 (
    .a(in_1), .b(or_1_out), .gt(comparator_1_gt));  // open: eq, lt
  Multiplexer #(.disabled("Z"), .width(32)) multiplexer_2 (
    .in0(subtractor_1_out), .in1(or_1_out), .out(out_4), .sel(comparator_1_gt));
  assign or_2_out = 32'h1 | shifter_3_out;  // OR_Gate or_2, 32 bits wide
endmodule

module Div32 (
  input  [31:0] d,
  input  [31:0] n2,
  output [31:0] rem,
  output [31:0] quot
);

  wire [31:0] l_32_div1_c33d2353_1_out_4, l_32_div1_c33d2353_1_out_5, l_32_div1_c33d2353_3_out_4,
       l_32_div1_c33d2353_3_out_5, l_32_div1_c33d2353_4_out_4, l_32_div1_c33d2353_4_out_5,
       l_32_div1_c33d2353_5_out_4, l_32_div1_c33d2353_5_out_5, l_32_div1_c33d2353_6_out_4,
       l_32_div1_c33d2353_6_out_5, l_32_div1_c33d2353_7_out_4, l_32_div1_c33d2353_7_out_5,
       l_32_div1_c33d2353_8_out_4, l_32_div1_c33d2353_8_out_5, l_32_div1_c33d2353_9_out_4,
       l_32_div1_c33d2353_9_out_5, l_32_div1_c33d2353_10_out_4, l_32_div1_c33d2353_10_out_5,
       l_32_div1_c33d2353_11_out_4, l_32_div1_c33d2353_11_out_5, l_32_div1_c33d2353_12_out_4,
       l_32_div1_c33d2353_12_out_5, l_32_div1_c33d2353_13_out_4, l_32_div1_c33d2353_13_out_5,
       l_32_div1_c33d2353_14_out_4, l_32_div1_c33d2353_14_out_5, l_32_div1_c33d2353_15_out_4,
       l_32_div1_c33d2353_15_out_5, l_32_div1_c33d2353_16_out_4, l_32_div1_c33d2353_16_out_5,
       l_32_div1_c33d2353_17_out_4, l_32_div1_c33d2353_17_out_5, l_32_div1_c33d2353_18_out_4,
       l_32_div1_c33d2353_18_out_5, l_32_div1_c33d2353_19_out_4, l_32_div1_c33d2353_19_out_5,
       l_32_div1_c33d2353_20_out_4, l_32_div1_c33d2353_20_out_5, l_32_div1_c33d2353_21_out_4,
       l_32_div1_c33d2353_21_out_5, l_32_div1_c33d2353_22_out_4, l_32_div1_c33d2353_22_out_5,
       l_32_div1_c33d2353_23_out_4, l_32_div1_c33d2353_23_out_5, l_32_div1_c33d2353_24_out_4,
       l_32_div1_c33d2353_24_out_5, l_32_div1_c33d2353_25_out_4, l_32_div1_c33d2353_25_out_5,
       l_32_div1_c33d2353_26_out_4, l_32_div1_c33d2353_26_out_5, l_32_div1_c33d2353_27_out_4,
       l_32_div1_c33d2353_27_out_5, l_32_div1_c33d2353_28_out_4, l_32_div1_c33d2353_28_out_5,
       l_32_div1_c33d2353_29_out_4, l_32_div1_c33d2353_29_out_5, l_32_div1_c33d2353_30_out_4,
       l_32_div1_c33d2353_30_out_5, l_32_div1_c33d2353_31_out_4, l_32_div1_c33d2353_31_out_5,
       l_32_div1_c33d2353_32_out_4, l_32_div1_c33d2353_32_out_5;

  L_32_div1_c33d2353 l_32_div1_c33d2353_1 (
    .in_3(l_32_div1_c33d2353_4_out_5), .in_2(l_32_div1_c33d2353_4_out_4), .in_1(d),
    .out_4(l_32_div1_c33d2353_1_out_4), .out_5(l_32_div1_c33d2353_1_out_5));
  L_32_div1_c33d2353 l_32_div1_c33d2353_2 (
    .in_3(l_32_div1_c33d2353_6_out_5), .in_2(l_32_div1_c33d2353_6_out_4), .in_1(d), .out_4(rem), .out_5(quot));
  L_32_div1_c33d2353 l_32_div1_c33d2353_3 (
    .in_3(n2), .in_2({32{1'b0}}), .in_1(d), .out_4(l_32_div1_c33d2353_3_out_4),
    .out_5(l_32_div1_c33d2353_3_out_5));
  L_32_div1_c33d2353 l_32_div1_c33d2353_4 (
    .in_3(l_32_div1_c33d2353_9_out_5), .in_2(l_32_div1_c33d2353_9_out_4), .in_1(d),
    .out_4(l_32_div1_c33d2353_4_out_4), .out_5(l_32_div1_c33d2353_4_out_5));
  L_32_div1_c33d2353 l_32_div1_c33d2353_5 (
    .in_3(l_32_div1_c33d2353_1_out_5), .in_2(l_32_div1_c33d2353_1_out_4), .in_1(d),
    .out_4(l_32_div1_c33d2353_5_out_4), .out_5(l_32_div1_c33d2353_5_out_5));
  L_32_div1_c33d2353 l_32_div1_c33d2353_6 (
    .in_3(l_32_div1_c33d2353_10_out_5), .in_2(l_32_div1_c33d2353_10_out_4), .in_1(d),
    .out_4(l_32_div1_c33d2353_6_out_4), .out_5(l_32_div1_c33d2353_6_out_5));
  L_32_div1_c33d2353 l_32_div1_c33d2353_7 (
    .in_3(l_32_div1_c33d2353_3_out_5), .in_2(l_32_div1_c33d2353_3_out_4), .in_1(d),
    .out_4(l_32_div1_c33d2353_7_out_4), .out_5(l_32_div1_c33d2353_7_out_5));
  L_32_div1_c33d2353 l_32_div1_c33d2353_8 (
    .in_3(l_32_div1_c33d2353_5_out_5), .in_2(l_32_div1_c33d2353_5_out_4), .in_1(d),
    .out_4(l_32_div1_c33d2353_8_out_4), .out_5(l_32_div1_c33d2353_8_out_5));
  L_32_div1_c33d2353 l_32_div1_c33d2353_9 (
    .in_3(l_32_div1_c33d2353_12_out_5), .in_2(l_32_div1_c33d2353_12_out_4), .in_1(d),
    .out_4(l_32_div1_c33d2353_9_out_4), .out_5(l_32_div1_c33d2353_9_out_5));
  L_32_div1_c33d2353 l_32_div1_c33d2353_10 (
    .in_3(l_32_div1_c33d2353_14_out_5), .in_2(l_32_div1_c33d2353_14_out_4), .in_1(d),
    .out_4(l_32_div1_c33d2353_10_out_4), .out_5(l_32_div1_c33d2353_10_out_5));
  L_32_div1_c33d2353 l_32_div1_c33d2353_11 (
    .in_3(l_32_div1_c33d2353_7_out_5), .in_2(l_32_div1_c33d2353_7_out_4), .in_1(d),
    .out_4(l_32_div1_c33d2353_11_out_4), .out_5(l_32_div1_c33d2353_11_out_5));
  L_32_div1_c33d2353 l_32_div1_c33d2353_12 (
    .in_3(l_32_div1_c33d2353_17_out_5), .in_2(l_32_div1_c33d2353_17_out_4), .in_1(d),
    .out_4(l_32_div1_c33d2353_12_out_4), .out_5(l_32_div1_c33d2353_12_out_5));
  L_32_div1_c33d2353 l_32_div1_c33d2353_13 (
    .in_3(l_32_div1_c33d2353_8_out_5), .in_2(l_32_div1_c33d2353_8_out_4), .in_1(d),
    .out_4(l_32_div1_c33d2353_13_out_4), .out_5(l_32_div1_c33d2353_13_out_5));
  L_32_div1_c33d2353 l_32_div1_c33d2353_14 (
    .in_3(l_32_div1_c33d2353_18_out_5), .in_2(l_32_div1_c33d2353_18_out_4), .in_1(d),
    .out_4(l_32_div1_c33d2353_14_out_4), .out_5(l_32_div1_c33d2353_14_out_5));
  L_32_div1_c33d2353 l_32_div1_c33d2353_15 (
    .in_3(l_32_div1_c33d2353_11_out_5), .in_2(l_32_div1_c33d2353_11_out_4), .in_1(d),
    .out_4(l_32_div1_c33d2353_15_out_4), .out_5(l_32_div1_c33d2353_15_out_5));
  L_32_div1_c33d2353 l_32_div1_c33d2353_16 (
    .in_3(l_32_div1_c33d2353_13_out_5), .in_2(l_32_div1_c33d2353_13_out_4), .in_1(d),
    .out_4(l_32_div1_c33d2353_16_out_4), .out_5(l_32_div1_c33d2353_16_out_5));
  L_32_div1_c33d2353 l_32_div1_c33d2353_17 (
    .in_3(l_32_div1_c33d2353_20_out_5), .in_2(l_32_div1_c33d2353_20_out_4), .in_1(d),
    .out_4(l_32_div1_c33d2353_17_out_4), .out_5(l_32_div1_c33d2353_17_out_5));
  L_32_div1_c33d2353 l_32_div1_c33d2353_18 (
    .in_3(l_32_div1_c33d2353_22_out_5), .in_2(l_32_div1_c33d2353_22_out_4), .in_1(d),
    .out_4(l_32_div1_c33d2353_18_out_4), .out_5(l_32_div1_c33d2353_18_out_5));
  L_32_div1_c33d2353 l_32_div1_c33d2353_19 (
    .in_3(l_32_div1_c33d2353_15_out_5), .in_2(l_32_div1_c33d2353_15_out_4), .in_1(d),
    .out_4(l_32_div1_c33d2353_19_out_4), .out_5(l_32_div1_c33d2353_19_out_5));
  L_32_div1_c33d2353 l_32_div1_c33d2353_20 (
    .in_3(l_32_div1_c33d2353_25_out_5), .in_2(l_32_div1_c33d2353_25_out_4), .in_1(d),
    .out_4(l_32_div1_c33d2353_20_out_4), .out_5(l_32_div1_c33d2353_20_out_5));
  L_32_div1_c33d2353 l_32_div1_c33d2353_21 (
    .in_3(l_32_div1_c33d2353_16_out_5), .in_2(l_32_div1_c33d2353_16_out_4), .in_1(d),
    .out_4(l_32_div1_c33d2353_21_out_4), .out_5(l_32_div1_c33d2353_21_out_5));
  L_32_div1_c33d2353 l_32_div1_c33d2353_22 (
    .in_3(l_32_div1_c33d2353_26_out_5), .in_2(l_32_div1_c33d2353_26_out_4), .in_1(d),
    .out_4(l_32_div1_c33d2353_22_out_4), .out_5(l_32_div1_c33d2353_22_out_5));
  L_32_div1_c33d2353 l_32_div1_c33d2353_23 (
    .in_3(l_32_div1_c33d2353_19_out_5), .in_2(l_32_div1_c33d2353_19_out_4), .in_1(d),
    .out_4(l_32_div1_c33d2353_23_out_4), .out_5(l_32_div1_c33d2353_23_out_5));
  L_32_div1_c33d2353 l_32_div1_c33d2353_24 (
    .in_3(l_32_div1_c33d2353_21_out_5), .in_2(l_32_div1_c33d2353_21_out_4), .in_1(d),
    .out_4(l_32_div1_c33d2353_24_out_4), .out_5(l_32_div1_c33d2353_24_out_5));
  L_32_div1_c33d2353 l_32_div1_c33d2353_25 (
    .in_3(l_32_div1_c33d2353_28_out_5), .in_2(l_32_div1_c33d2353_28_out_4), .in_1(d),
    .out_4(l_32_div1_c33d2353_25_out_4), .out_5(l_32_div1_c33d2353_25_out_5));
  L_32_div1_c33d2353 l_32_div1_c33d2353_26 (
    .in_3(l_32_div1_c33d2353_30_out_5), .in_2(l_32_div1_c33d2353_30_out_4), .in_1(d),
    .out_4(l_32_div1_c33d2353_26_out_4), .out_5(l_32_div1_c33d2353_26_out_5));
  L_32_div1_c33d2353 l_32_div1_c33d2353_27 (
    .in_3(l_32_div1_c33d2353_23_out_5), .in_2(l_32_div1_c33d2353_23_out_4), .in_1(d),
    .out_4(l_32_div1_c33d2353_27_out_4), .out_5(l_32_div1_c33d2353_27_out_5));
  L_32_div1_c33d2353 l_32_div1_c33d2353_28 (
    .in_3(l_32_div1_c33d2353_31_out_5), .in_2(l_32_div1_c33d2353_31_out_4), .in_1(d),
    .out_4(l_32_div1_c33d2353_28_out_4), .out_5(l_32_div1_c33d2353_28_out_5));
  L_32_div1_c33d2353 l_32_div1_c33d2353_29 (
    .in_3(l_32_div1_c33d2353_24_out_5), .in_2(l_32_div1_c33d2353_24_out_4), .in_1(d),
    .out_4(l_32_div1_c33d2353_29_out_4), .out_5(l_32_div1_c33d2353_29_out_5));
  L_32_div1_c33d2353 l_32_div1_c33d2353_30 (
    .in_3(l_32_div1_c33d2353_32_out_5), .in_2(l_32_div1_c33d2353_32_out_4), .in_1(d),
    .out_4(l_32_div1_c33d2353_30_out_4), .out_5(l_32_div1_c33d2353_30_out_5));
  L_32_div1_c33d2353 l_32_div1_c33d2353_31 (
    .in_3(l_32_div1_c33d2353_27_out_5), .in_2(l_32_div1_c33d2353_27_out_4), .in_1(d),
    .out_4(l_32_div1_c33d2353_31_out_4), .out_5(l_32_div1_c33d2353_31_out_5));
  L_32_div1_c33d2353 l_32_div1_c33d2353_32 (
    .in_3(l_32_div1_c33d2353_29_out_5), .in_2(l_32_div1_c33d2353_29_out_4), .in_1(d),
    .out_4(l_32_div1_c33d2353_32_out_4), .out_5(l_32_div1_c33d2353_32_out_5));
endmodule

module sDiv32 (
  input  [31:0] A,
  input  [31:0] B,
  output [31:0] out_3
);

  wire xor_3_out;
  wire [31:0] bit_extender_1_out, bit_extender_2_out, bit_extender_3_out, bit_extender_4_out,
       bit_extender_5_out, bit_extender_6_out, div32_1_p3, plus32_1_s, plus32_2_s, xor_1_out, xor_2_out,
       xor_4_out;

  assign bit_extender_1_out = {{31{1'b0}}, A[31]};  // Bit_Extender bit_extender_1
  assign bit_extender_2_out = {{31{A[31]}}, A[31]};  // Bit_Extender bit_extender_2
  assign bit_extender_3_out = {{31{1'b0}}, B[31]};  // Bit_Extender bit_extender_3
  assign bit_extender_4_out = {{31{B[31]}}, B[31]};  // Bit_Extender bit_extender_4
  assign xor_1_out = bit_extender_2_out ^ A;  // XOR_Gate xor_1, 32 bits wide
  assign xor_2_out = bit_extender_4_out ^ B;  // XOR_Gate xor_2, 32 bits wide
  plus32 plus32_1 (.A(bit_extender_1_out), .B(xor_1_out), .S(plus32_1_s));  // open: SUB, C
  plus32 plus32_2 (.A(bit_extender_3_out), .B(xor_2_out), .S(plus32_2_s));  // open: SUB, C
  // Div32 div32_1: pin names not known; wires that end beside it: plus32_1_s, plus32_2_s, div32_1_p3
  xor xor_3 (xor_3_out, A[31], B[31]);
  assign bit_extender_5_out = {{31{xor_3_out}}, xor_3_out};  // Bit_Extender bit_extender_5
  assign bit_extender_6_out = {{31{1'b0}}, xor_3_out};  // Bit_Extender bit_extender_6
  assign xor_4_out = div32_1_p3 ^ bit_extender_5_out;  // XOR_Gate xor_4, 32 bits wide
  plus32 plus32_3 (.A(xor_4_out), .B(bit_extender_6_out), .S(out_3));  // open: SUB, C
endmodule
